// Logisim project Ivan (2).circ as structural Verilog: 28 circuits, main circuit main
module main (
);

  wire ALU_zero, button_1_out, clock_1_out, Decoder_halt, Decoder_immtoalu, Decoder_immtopc, Decoder_led,
       Decoder_memread, Decoder_memtoreg, Decoder_memwrite, Decoder_pctoreg, Decoder_regtopc,
       Decoder_regwrite, Decoder_shiftertoreg, Decoder_shiftsrc, Decoder_writeled, Decoder_zerostoalu,
       Instruction_Splitter_subop, Instruction_Splitter_unsigned, not_1_out, ResultToLess_less;
  wire [2:0] Instruction_Splitter_readregister1, Instruction_Splitter_readregister2,
       Instruction_Splitter_writeregister;
  wire [3:0] Decoder_aluop, Instruction_Splitter_opcode, Instruction_Splitter_shiftamount;
  wire [7:0] adder_1_out, Instruction_Splitter_immediate, multiplexer_3_out, multiplexer_4_out, PC_q,
       RegistertoAddress_2_address, RegistertoAddress_address;
  wire [15:0] ALU_result, bit_extender_1_out, multiplexer_1_out, multiplexer_2_out, multiplexer_5_out,
       multiplexer_6_out, multiplexer_7_out, ram_1_data, register_1_q, Registers_readdata1,
       Registers_readdata2, rom_1_data, Shifter_shiftout, Sign_Extend_signextendedimm;

  not not_1 (not_1_out, Decoder_halt);
  Clock clock_1 (.out(clock_1_out));
  Register PC (.D(multiplexer_4_out), .en(not_1_out), .Q(PC_q), .clk(clock_1_out), .clr(button_1_out));
  Button button_1 (.out(button_1_out));
  Adder adder_1 (.a(PC_q), .b(8'h1), .out(adder_1_out));  // open: cin, cout
  ROM #(.dataWidth(16)) rom_1 (.addr(PC_q), .data(rom_1_data), .sel(1'b1));
  InstructionSplitter Instruction_Splitter (
    .Instruction(rom_1_data), .Opcode(Instruction_Splitter_opcode),
    .ReadRegister1(Instruction_Splitter_readregister1), .ReadRegister2(Instruction_Splitter_readregister2),
    .WriteRegister(Instruction_Splitter_writeregister), .ShiftAmount(Instruction_Splitter_shiftamount),
    .SubOp(Instruction_Splitter_subop), .Unsigned(Instruction_Splitter_unsigned),
    .Immediate(Instruction_Splitter_immediate));
  SignExtend Sign_Extend (
    .Unsigned(Instruction_Splitter_unsigned), .Immediate(Instruction_Splitter_immediate),
    .SignExtendedImm(Sign_Extend_signextendedimm));
  ResultToLess ResultToLess (.Result(ALU_result), .Less(ResultToLess_less));
  RegisterFile Registers (
    .ReadRegister1(Instruction_Splitter_readregister1), .ReadRegister2(Instruction_Splitter_readregister2),
    .WriteRegister(Instruction_Splitter_writeregister), .WriteData(multiplexer_5_out),
    .WriteEnable(Decoder_regwrite), .Clock(clock_1_out), .ReadData1(Registers_readdata1),
    .ReadData2(Registers_readdata2));
  Decoder Decoder (
    .Opcode(Instruction_Splitter_opcode), .Subop(Instruction_Splitter_subop), .Zero(ALU_zero),
    .Less(ResultToLess_less), .ShiftSrc(Decoder_shiftsrc), .ShifterToReg(Decoder_shiftertoreg),
    .RegWrite(Decoder_regwrite), .ALUOp(Decoder_aluop), .IMMtoALU(Decoder_immtoalu),
    .RegtoPC(Decoder_regtopc), .IMMtoPC(Decoder_immtopc), .ZerosToALU(Decoder_zerostoalu),
    .MemWrite(Decoder_memwrite), .MemtoReg(Decoder_memtoreg), .Halt(Decoder_halt), .LED(Decoder_led),
    .WriteLED(Decoder_writeled), .MemRead(Decoder_memread), .PCtoReg(Decoder_pctoreg));
  Multiplexer #(.width(16), .disabled(0), .enable("false")) multiplexer_1 (
    .in0(Registers_readdata2), .in1(Sign_Extend_signextendedimm), .out(multiplexer_1_out),
    .sel(Decoder_immtoalu));
  ALUtoPC RegistertoAddress (.ALUOut(Registers_readdata1), .Address(RegistertoAddress_address));
  Multiplexer #(.width(16), .disabled(0), .enable("false")) multiplexer_2 (
    .in0(multiplexer_1_out), .in1({16{1'b0}}), .out(multiplexer_2_out), .sel(Decoder_zerostoalu));
  Multiplexer #(.width(8), .disabled(0), .enable("false")) multiplexer_3 (
    .in0(adder_1_out), .in1(Instruction_Splitter_immediate), .out(multiplexer_3_out), .sel(Decoder_immtopc));
  sixteen_bit_ALU ALU (
    .ALUOperation(Decoder_aluop), .a(Registers_readdata1), .b(multiplexer_2_out), .Zero(ALU_zero),
    .Result(ALU_result));  // open: Overflow
  Multiplexer #(.width(8), .disabled(0), .enable("false")) multiplexer_4 (
    .in0(multiplexer_3_out), .in1(RegistertoAddress_address), .out(multiplexer_4_out), .sel(Decoder_regtopc));
  ALUtoPC RegistertoAddress_2 (.ALUOut(Registers_readdata2), .Address(RegistertoAddress_2_address));
  Multiplexer #(.width(16), .disabled(0), .enable("false")) multiplexer_5 (
    .in0(multiplexer_6_out), .in1(bit_extender_1_out), .out(multiplexer_5_out), .sel(Decoder_pctoreg));
  Shifter Shifter (
    .Subop(Instruction_Splitter_subop), .Data(Registers_readdata1), .ShamtReg(Registers_readdata2),
    .ShiftSrc(Decoder_shiftsrc), .Shamt(Instruction_Splitter_shiftamount), .ShiftOut(Shifter_shiftout));
  assign bit_extender_1_out = {{8{1'b0}}, adder_1_out};  // Bit_Extender bit_extender_1
  Multiplexer #(.width(16), .disabled(0), .enable("false")) multiplexer_6 (
    .in0(multiplexer_7_out), .in1(Shifter_shiftout), .out(multiplexer_6_out), .sel(Decoder_shiftertoreg));
  RAM #(.dataWidth(16), .bus("separate")) ram_1 (
    .addr(RegistertoAddress_2_address), .din(Registers_readdata1), .data(ram_1_data), .str(Decoder_memwrite),
    .sel(1'b1), .clk(clock_1_out), .ld(Decoder_memread));  // open: clr
  Multiplexer #(.width(16), .disabled(0), .enable("false")) multiplexer_7 (
    .in0(ALU_result), .in1(ram_1_data), .out(multiplexer_7_out), .sel(Decoder_memtoreg));
  Hex_Digit_Display hex_digit_display_1 (.value(register_1_q[15:12]));  // open: dp
  Register #(.width(16)) register_1 (
    .D(Registers_readdata1), .en(Decoder_writeled), .Q(register_1_q), .clk(clock_1_out));  // open: clr
  LED Halt (.in(Decoder_led));
  Hex_Digit_Display hex_digit_display_2 (.value(register_1_q[11:8]));  // open: dp
  Hex_Digit_Display hex_digit_display_3 (.value(register_1_q[7:4]));  // open: dp
  Hex_Digit_Display hex_digit_display_4 (.value(register_1_q[3:0]));  // open: dp

  // Notes on the sheet:
  //   contents of rom_1 (hex, n*v repeats v):
  //   16f6 1904 1206 1afe 1d03 8c0 22c0 b00 f600 f200 f800 fa00 7000
endmodule

module InstructionSplitter (
  input  [15:0] Instruction,
  output [3:0] Opcode,
  output [2:0] ReadRegister1,
  output [2:0] ReadRegister2,
  output [2:0] WriteRegister,
  output [3:0] ShiftAmount,
  output SubOp,
  output Unsigned,
  output [7:0] Immediate
);


  assign Immediate = Instruction[7:0];
  assign Opcode = Instruction[15:12];
  assign ReadRegister1 = Instruction[11:9];
  assign ReadRegister2 = Instruction[8:6];
  assign ShiftAmount = Instruction[4:1];
  assign SubOp = Instruction[0];
  assign Unsigned = Instruction[8];
  assign WriteRegister = Instruction[11:9];
endmodule

module SignExtend (
  input  Unsigned,
  input  [7:0] Immediate,
  output [15:0] SignExtendedImm
);

  wire [15:0] bit_extender_1_out, bit_extender_2_out;

  assign bit_extender_1_out = {{8{Immediate[7]}}, Immediate};  // Bit_Extender bit_extender_1
  assign bit_extender_2_out = {{8{1'b0}}, Immediate};  // Bit_Extender bit_extender_2
  Multiplexer #(.width(16), .disabled(0), .enable("false")) multiplexer_1 (
    .in0(bit_extender_1_out), .in1(bit_extender_2_out), .out(SignExtendedImm), .sel(Unsigned));
endmodule

module ALUtoPC (
  input  [15:0] ALUOut,
  output [7:0] Address
);


  assign Address = ALUOut[7:0];
endmodule

module Shifter (
  input  Subop,
  input  [15:0] Data,
  input  [15:0] ShamtReg,
  input  ShiftSrc,
  input  [3:0] Shamt,
  output [15:0] ShiftOut
);

  wire [3:0] multiplexer_1_out;
  wire [15:0] shifter_1_out, shifter_2_out;

  Multiplexer #(.width(4), .disabled(0), .enable("false")) multiplexer_1 (
    .in0(ShamtReg[3:0]), .in1(Shamt), .out(multiplexer_1_out), .sel(ShiftSrc));
  Shifter_part #(.width(16)) shifter_1 (.in(Data), .\dist (multiplexer_1_out), .out(shifter_1_out));
  Shifter_part #(.width(16), .shift("lr")) shifter_2 (.in(Data), .\dist (multiplexer_1_out), .out(shifter_2_out));
  Multiplexer #(.width(16), .disabled(0), .enable("false")) multiplexer_2 (
    .in0(shifter_1_out), .in1(shifter_2_out), .out(ShiftOut), .sel(Subop));
endmodule

module RegisterFile (
  input  [2:0] ReadRegister1,
  input  [2:0] ReadRegister2,
  input  [2:0] WriteRegister,
  input  [15:0] WriteData,
  input  WriteEnable,
  input  Clock,
  output [15:0] ReadData1,
  output [15:0] ReadData2
);

  wire decoder_1_out0, decoder_1_out1, decoder_1_out2, decoder_1_out3, decoder_1_out4, decoder_1_out5,
       decoder_1_out6, decoder_1_out7;
  wire [15:0] register_1_q, register_2_q, register_3_q, register_4_q, register_5_q, register_6_q,
       register_7_q, register_8_q;

  Decoder_part #(.select(3), .disabled(0)) decoder_1 (
    .out0(decoder_1_out0), .out1(decoder_1_out1), .out2(decoder_1_out2), .out3(decoder_1_out3),
    .out4(decoder_1_out4), .out5(decoder_1_out5), .out6(decoder_1_out6), .out7(decoder_1_out7),
    .sel(WriteRegister), .en(WriteEnable));
  Register #(.width(16)) register_1 (.D(WriteData), .en(decoder_1_out0), .Q(register_1_q), .clk(Clock));  // open: clr
  Register #(.width(16)) register_2 (.D(WriteData), .en(decoder_1_out1), .Q(register_2_q), .clk(Clock));  // open: clr
  Register #(.width(16)) register_3 (.D(WriteData), .en(decoder_1_out2), .Q(register_3_q), .clk(Clock));  // open: clr
  Register #(.width(16)) register_4 (.D(WriteData), .en(decoder_1_out3), .Q(register_4_q), .clk(Clock));  // open: clr
  Register #(.width(16)) register_5 (.D(WriteData), .en(decoder_1_out4), .Q(register_5_q), .clk(Clock));  // open: clr
  Register #(.width(16)) register_6 (.D(WriteData), .en(decoder_1_out5), .Q(register_6_q), .clk(Clock));  // open: clr
  Register #(.width(16)) register_7 (.D(WriteData), .en(decoder_1_out6), .Q(register_7_q), .clk(Clock));  // open: clr
  Register #(.width(16)) register_8 (.D(WriteData), .en(decoder_1_out7), .Q(register_8_q), .clk(Clock));  // open: clr
  Multiplexer #(.select(3), .width(16), .enable("false")) multiplexer_1 (
    .in0(register_1_q), .in1(register_2_q), .in2(register_3_q), .in3(register_4_q), .in4(register_5_q),
    .in5(register_6_q), .in6(register_7_q), .in7(register_8_q), .out(ReadData1), .sel(ReadRegister1));
  Multiplexer #(.select(3), .width(16), .enable("false")) multiplexer_2 (
    .in0(register_1_q), .in1(register_2_q), .in2(register_3_q), .in3(register_4_q), .in4(register_5_q),
    .in5(register_6_q), .in6(register_7_q), .in7(register_8_q), .out(ReadData2), .sel(ReadRegister2));
endmodule

module ShifterDecoder (
  input  [3:0] Opcode,
  output ShiftSrc,
  output ShiftertoReg,
  output RegWrite
);

  and and_1 (RegWrite, ~Opcode[3], Opcode[2], ~Opcode[1]);  // AND_Gate

  assign ShiftertoReg = RegWrite;
  assign ShiftSrc = Opcode[0];
endmodule

module Arith_Log_Decoder (
  input  [3:0] Opcode,
  input  Subop,
  output [3:0] ALUOperation,
  output RegWrite,
  output ALUSrc
);

  wire and_1_out, and_3_out, and_4_out, and_5_out, and_6_out, and_7_out, not_1_out, not_2_out, not_3_out,
       not_4_out, not_5_out, not_6_out, not_7_out, not_8_out, not_9_out, not_10_out, not_11_out, not_12_out,
       not_13_out, not_14_out, not_15_out, not_16_out, not_17_out, not_18_out, not_19_out, not_20_out,
       not_21_out;

  and and_1 (and_1_out, ~Opcode[3], ~Opcode[2], Opcode[1], ~Opcode[0], ~Subop);  // AND_Gate
  not not_1 (not_1_out, Opcode[3]);
  not not_2 (not_2_out, Opcode[2]);
  not not_3 (not_3_out, Subop);
  not not_4 (not_4_out, Opcode[3]);
  not not_5 (not_5_out, Opcode[2]);
  not not_6 (not_6_out, Opcode[1]);
  not not_7 (not_7_out, Opcode[0]);
  not not_8 (not_8_out, Opcode[3]);
  not not_9 (not_9_out, Opcode[2]);
  not not_10 (not_10_out, Subop);
  not not_11 (not_11_out, Opcode[3]);
  not not_12 (not_12_out, Opcode[2]);
  not not_13 (not_13_out, Opcode[1]);
  not not_14 (not_14_out, Opcode[3]);
  not not_15 (not_15_out, Opcode[2]);
  not not_16 (not_16_out, Opcode[1]);
  not not_17 (not_17_out, Opcode[3]);
  not not_18 (not_18_out, Opcode[2]);
  not not_19 (not_19_out, Opcode[3]);
  not not_20 (not_20_out, Opcode[2]);
  not not_21 (not_21_out, Opcode[1]);
  and and_2 (ALUOperation[3], not_1_out, not_2_out, Opcode[1], Opcode[0], not_3_out);
  and and_3 (and_3_out, not_4_out, not_5_out, not_6_out, not_7_out, Subop);
  and and_4 (and_4_out, not_8_out, not_9_out, Opcode[1], Opcode[0], not_10_out);
  and and_5 (and_5_out, not_11_out, not_12_out, not_13_out);
  and and_6 (and_6_out, not_14_out, not_15_out, not_16_out);
  and and_7 (and_7_out, not_17_out, not_18_out, Opcode[0]);
  and and_8 (ALUSrc, not_19_out, not_20_out, not_21_out, Opcode[0]);
  or or_1 (ALUOperation[2], and_3_out, and_1_out, and_4_out);
  or or_2 (ALUOperation[1], and_1_out, and_5_out);
  or or_3 (RegWrite, and_6_out, and_7_out);

  assign ALUOperation[0] = 1'b0;

  // Notes on the sheet:
  //   SUB
  //   SUB
endmodule

module Arith_Log (
  input  Opcode3,
  input  Opcode2,
  input  Opcode1,
  input  Opcode0,
  input  Unsigned,
  input  Subop,
  output ALUOp3,
  output ALUOp2,
  output ALUOp1,
  output ALUOp0,
  output RegWrite,
  output ALUSrc
);

  wire and_2_out, and_3_out, and_5_out, and_6_out, not_1_out, not_2_out, not_3_out, not_4_out, not_5_out,
       not_6_out, not_7_out, not_8_out, not_9_out, not_10_out, not_11_out, not_12_out, not_13_out,
       not_14_out, not_15_out, not_16_out, not_17_out, not_18_out, not_19_out, not_20_out, not_21_out;

  not not_1 (not_1_out, Opcode3);
  not not_2 (not_2_out, Opcode2);
  not not_3 (not_3_out, Subop);
  not not_4 (not_4_out, Opcode3);
  not not_5 (not_5_out, Opcode2);
  not not_6 (not_6_out, Opcode1);
  not not_7 (not_7_out, Opcode0);
  not not_8 (not_8_out, Opcode3);
  not not_9 (not_9_out, Opcode2);
  not not_10 (not_10_out, Subop);
  not not_11 (not_11_out, Opcode3);
  not not_12 (not_12_out, Opcode2);
  not not_13 (not_13_out, Opcode1);
  not not_14 (not_14_out, Opcode3);
  not not_15 (not_15_out, Opcode2);
  not not_16 (not_16_out, Opcode1);
  not not_17 (not_17_out, Opcode3);
  not not_18 (not_18_out, Opcode2);
  not not_19 (not_19_out, Opcode3);
  not not_20 (not_20_out, Opcode2);
  not not_21 (not_21_out, Opcode1);
  and and_1 (ALUOp3, not_1_out, not_2_out, Opcode1, Opcode0, not_3_out);
  and and_2 (and_2_out, not_4_out, not_5_out, not_6_out, not_7_out, Subop);
  and and_3 (and_3_out, not_8_out, not_9_out, Opcode1, Opcode0, not_10_out);
  and and_4 (ALUOp1, not_11_out, not_12_out, not_13_out);
  and and_5 (and_5_out, not_14_out, not_15_out, not_16_out);
  and and_6 (and_6_out, not_17_out, not_18_out, Opcode0);
  and and_7 (ALUSrc, not_19_out, not_20_out, not_21_out, Opcode0);
  or or_1 (ALUOp2, and_2_out, and_3_out);
  or or_2 (RegWrite, and_5_out, and_6_out);

  assign ALUOp0 = 1'b0;
endmodule

module one_bit_ALU (
  input  Ainvert,
  input  Binvert,
  input  CarryIn,
  input  [1:0] Operation,
  input  a,
  input  b,
  input  Less,
  output Result,
  output Set,
  output CarryOut
);

  wire and_1_out, multiplexer_1_out, multiplexer_2_out, not_1_out, not_2_out, or_1_out;

  not not_1 (not_1_out, a);
  Multiplexer #(.enable("false")) multiplexer_1 (.in0(a), .in1(not_1_out), .out(multiplexer_1_out), .sel(Ainvert));
  not not_2 (not_2_out, b);
  Multiplexer #(.enable("false")) multiplexer_2 (.in0(b), .in1(not_2_out), .out(multiplexer_2_out), .sel(Binvert));
  and and_1 (and_1_out, multiplexer_1_out, multiplexer_2_out);
  or or_1 (or_1_out, multiplexer_1_out, multiplexer_2_out);
  Adder #(.width(1)) adder_1 (.a(multiplexer_1_out), .b(multiplexer_2_out), .out(Set), .cin(CarryIn), .cout(CarryOut));
  Multiplexer #(.select(2), .enable("false")) multiplexer_3 (
    .in0(and_1_out), .in1(or_1_out), .in2(Set), .in3(Less), .out(Result), .sel(Operation));
endmodule

module sixteen_bit_ALU (
  input  [3:0] ALUOperation,
  input  [15:0] a,
  input  [15:0] b,
  output Zero,
  output [15:0] Result,
  output Overflow
);

  wire one_bit_alu_1_carryout, one_bit_alu_2_carryout, one_bit_alu_3_carryout, one_bit_alu_4_carryout,
       one_bit_alu_5_carryout, one_bit_alu_6_carryout, one_bit_alu_7_carryout, one_bit_alu_8_carryout,
       one_bit_alu_9_carryout, one_bit_alu_10_carryout, one_bit_alu_11_carryout, one_bit_alu_12_carryout,
       one_bit_alu_13_carryout, one_bit_alu_14_carryout, one_bit_alu_15_carryout, one_bit_alu_16_carryout,
       one_bit_alu_16_set, xor_1_out;

  one_bit_ALU one_bit_alu_1 (
    .a(a[0]), .b(b[0]), .Less(xor_1_out), .Ainvert(ALUOperation[3]), .Binvert(ALUOperation[2]),
    .CarryIn(ALUOperation[2]), .Operation(ALUOperation[1:0]), .CarryOut(one_bit_alu_1_carryout),
    .Result(Result[0]));  // open: Set
  one_bit_ALU one_bit_alu_2 (
    .a(a[1]), .b(b[1]), .Less(1'b0), .Ainvert(ALUOperation[3]), .Binvert(ALUOperation[2]),
    .CarryIn(one_bit_alu_1_carryout), .Operation(ALUOperation[1:0]), .CarryOut(one_bit_alu_2_carryout),
    .Result(Result[1]));  // open: Set
  one_bit_ALU one_bit_alu_3 (
    .a(a[2]), .b(b[2]), .Less(1'b0), .Ainvert(ALUOperation[3]), .Binvert(ALUOperation[2]),
    .CarryIn(one_bit_alu_2_carryout), .Operation(ALUOperation[1:0]), .CarryOut(one_bit_alu_3_carryout),
    .Result(Result[2]));  // open: Set
  one_bit_ALU one_bit_alu_4 (
    .a(a[3]), .b(b[3]), .Less(1'b0), .Ainvert(ALUOperation[3]), .Binvert(ALUOperation[2]),
    .CarryIn(one_bit_alu_3_carryout), .Operation(ALUOperation[1:0]), .CarryOut(one_bit_alu_4_carryout),
    .Result(Result[3]));  // open: Set
  one_bit_ALU one_bit_alu_5 (
    .a(a[4]), .b(b[4]), .Less(1'b0), .Ainvert(ALUOperation[3]), .Binvert(ALUOperation[2]),
    .CarryIn(one_bit_alu_4_carryout), .Operation(ALUOperation[1:0]), .CarryOut(one_bit_alu_5_carryout),
    .Result(Result[4]));  // open: Set
  one_bit_ALU one_bit_alu_6 (
    .a(a[5]), .b(b[5]), .Less(1'b0), .Ainvert(ALUOperation[3]), .Binvert(ALUOperation[2]),
    .CarryIn(one_bit_alu_5_carryout), .Operation(ALUOperation[1:0]), .CarryOut(one_bit_alu_6_carryout),
    .Result(Result[5]));  // open: Set
  one_bit_ALU one_bit_alu_7 (
    .a(a[6]), .b(b[6]), .Less(1'b0), .Ainvert(ALUOperation[3]), .Binvert(ALUOperation[2]),
    .CarryIn(one_bit_alu_6_carryout), .Operation(ALUOperation[1:0]), .CarryOut(one_bit_alu_7_carryout),
    .Result(Result[6]));  // open: Set
  one_bit_ALU one_bit_alu_8 (
    .a(a[7]), .b(b[7]), .Less(1'b0), .Ainvert(ALUOperation[3]), .Binvert(ALUOperation[2]),
    .CarryIn(one_bit_alu_7_carryout), .Operation(ALUOperation[1:0]), .CarryOut(one_bit_alu_8_carryout),
    .Result(Result[7]));  // open: Set
  one_bit_ALU one_bit_alu_9 (
    .a(a[8]), .b(b[8]), .Less(1'b0), .Ainvert(ALUOperation[3]), .Binvert(ALUOperation[2]),
    .CarryIn(one_bit_alu_8_carryout), .Operation(ALUOperation[1:0]), .CarryOut(one_bit_alu_9_carryout),
    .Result(Result[8]));  // open: Set
  one_bit_ALU one_bit_alu_10 (
    .a(a[9]), .b(b[9]), .Less(1'b0), .Ainvert(ALUOperation[3]), .Binvert(ALUOperation[2]),
    .CarryIn(one_bit_alu_9_carryout), .Operation(ALUOperation[1:0]), .CarryOut(one_bit_alu_10_carryout),
    .Result(Result[9]));  // open: Set
  one_bit_ALU one_bit_alu_11 (
    .a(a[10]), .b(b[10]), .Less(1'b0), .Ainvert(ALUOperation[3]), .Binvert(ALUOperation[2]),
    .CarryIn(one_bit_alu_10_carryout), .Operation(ALUOperation[1:0]), .CarryOut(one_bit_alu_11_carryout),
    .Result(Result[10]));  // open: Set
  one_bit_ALU one_bit_alu_12 (
    .a(a[11]), .b(b[11]), .Less(1'b0), .Ainvert(ALUOperation[3]), .Binvert(ALUOperation[2]),
    .CarryIn(one_bit_alu_11_carryout), .Operation(ALUOperation[1:0]), .CarryOut(one_bit_alu_12_carryout),
    .Result(Result[11]));  // open: Set
  one_bit_ALU one_bit_alu_13 (
    .a(a[12]), .b(b[12]), .Less(1'b0), .Ainvert(ALUOperation[3]), .Binvert(ALUOperation[2]),
    .CarryIn(one_bit_alu_12_carryout), .Operation(ALUOperation[1:0]), .CarryOut(one_bit_alu_13_carryout),
    .Result(Result[12]));  // open: Set
  one_bit_ALU one_bit_alu_14 (
    .a(a[13]), .b(b[13]), .Less(1'b0), .Ainvert(ALUOperation[3]), .Binvert(ALUOperation[2]),
    .CarryIn(one_bit_alu_13_carryout), .Operation(ALUOperation[1:0]), .CarryOut(one_bit_alu_14_carryout),
    .Result(Result[13]));  // open: Set
  one_bit_ALU one_bit_alu_15 (
    .a(a[14]), .b(b[14]), .Less(1'b0), .Ainvert(ALUOperation[3]), .Binvert(ALUOperation[2]),
    .CarryIn(one_bit_alu_14_carryout), .Operation(ALUOperation[1:0]), .CarryOut(one_bit_alu_15_carryout),
    .Result(Result[14]));  // open: Set
  one_bit_ALU one_bit_alu_16 (
    .a(a[15]), .b(b[15]), .Less(1'b0), .Ainvert(ALUOperation[3]), .Binvert(ALUOperation[2]),
    .CarryIn(one_bit_alu_15_carryout), .Operation(ALUOperation[1:0]), .CarryOut(one_bit_alu_16_carryout),
    .Result(Result[15]), .Set(one_bit_alu_16_set));
  xor xor_1 (xor_1_out, one_bit_alu_16_set, Overflow);
  xor xor_2 (Overflow, one_bit_alu_15_carryout, one_bit_alu_16_carryout);
  nor nor_1 (Zero, Result[0], Result[1], Result[2], Result[3], Result[4], Result[5], Result[6], Result[7], Result[8], Result[9], Result[10], Result[11], Result[12], Result[13], Result[14], Result[15]);
endmodule

module PCDecoder (
  input  [3:0] Opcode,
  input  Subop,
  input  Zero,
  input  Less,
  output RegtoPC,
  output IMMtoPC,
  output ZerosToALU,
  output [3:0] ALUOp
);

  wire and_4_out, and_5_out, and_6_out, and_7_out, and_8_out, not_1_out, not_2_out, not_3_out, not_4_out,
       not_5_out, not_6_out, not_7_out, not_8_out, not_9_out, not_10_out, not_11_out, not_12_out, not_13_out,
       not_14_out, not_15_out, not_16_out;

  not not_1 (not_1_out, Opcode[2]);
  not not_2 (not_2_out, Opcode[1]);
  not not_3 (not_3_out, Subop);
  not not_4 (not_4_out, Opcode[2]);
  not not_5 (not_5_out, Opcode[1]);
  not not_6 (not_6_out, Opcode[0]);
  not not_7 (not_7_out, Opcode[2]);
  not not_8 (not_8_out, Opcode[1]);
  not not_9 (not_9_out, Zero);
  not not_10 (not_10_out, Opcode[2]);
  not not_11 (not_11_out, Zero);
  not not_12 (not_12_out, Opcode[0]);
  not not_13 (not_13_out, Zero);
  not not_14 (not_14_out, Less);
  not not_15 (not_15_out, Opcode[0]);
  and and_1 (ZerosToALU, Opcode[3], not_16_out);
  not not_16 (not_16_out, Opcode[2]);
  and and_2 (ALUOp[1], Opcode[3], not_1_out);
  and and_3 (RegtoPC, Opcode[3], Opcode[2], not_2_out, Opcode[0], not_3_out);
  and and_4 (and_4_out, Opcode[3], not_4_out, not_5_out, not_6_out, Zero);
  and and_5 (and_5_out, Opcode[3], not_7_out, not_8_out, Opcode[0], not_9_out);
  and and_6 (and_6_out, Opcode[3], not_10_out, Opcode[0], not_11_out, Less);
  and and_7 (and_7_out, Opcode[3], Opcode[1], not_12_out, not_13_out, not_14_out);
  and and_8 (and_8_out, Opcode[3], Opcode[2], Opcode[1], not_15_out);
  or or_1 (IMMtoPC, and_4_out, and_5_out, and_6_out, and_7_out, and_8_out);

  assign {ALUOp[3:2], ALUOp[0]} = 3'b000;
endmodule

module PCDecoderLogic (
  input  Opcode3,
  input  Opcode2,
  input  Opcode1,
  input  Opcode0,
  input  Subop,
  input  Zero,
  input  Less,
  output RegtoPC,
  output IMMtoPC,
  output OnestoALU
);

  wire and_2_out, and_3_out, and_4_out, and_5_out, and_6_out, not_1_out, not_2_out, not_3_out, not_4_out,
       not_5_out, not_6_out, not_7_out, not_8_out, not_9_out, not_10_out, not_11_out, not_12_out, not_13_out,
       not_14_out, not_15_out;

  not not_1 (not_1_out, Opcode1);
  not not_2 (not_2_out, Subop);
  not not_3 (not_3_out, Opcode2);
  not not_4 (not_4_out, Opcode1);
  not not_5 (not_5_out, Opcode0);
  not not_6 (not_6_out, Opcode2);
  not not_7 (not_7_out, Opcode1);
  not not_8 (not_8_out, Zero);
  not not_9 (not_9_out, Opcode2);
  not not_10 (not_10_out, Zero);
  not not_11 (not_11_out, Opcode0);
  not not_12 (not_12_out, Zero);
  not not_13 (not_13_out, Less);
  not not_14 (not_14_out, Opcode0);
  not not_15 (not_15_out, Opcode2);
  and and_1 (RegtoPC, Opcode3, Opcode2, not_1_out, Opcode0, not_2_out);
  and and_2 (and_2_out, Opcode3, not_3_out, not_4_out, not_5_out, Zero);
  and and_3 (and_3_out, Opcode3, not_6_out, not_7_out, Opcode0, not_8_out);
  and and_4 (and_4_out, Opcode3, not_9_out, Opcode0, not_10_out, Less);
  and and_5 (and_5_out, Opcode3, Opcode1, not_11_out, not_12_out, not_13_out);
  and and_6 (and_6_out, Opcode3, Opcode2, Opcode1, not_14_out);
  and and_7 (OnestoALU, Opcode3, not_15_out);
  or or_1 (IMMtoPC, and_2_out, and_3_out, and_4_out, and_5_out, and_6_out);
endmodule

module Decoder (
  input  [3:0] Opcode,
  input  Subop,
  input  Zero,
  input  Less,
  output ShiftSrc,
  output ShifterToReg,
  output RegWrite,
  output [3:0] ALUOp,
  output IMMtoALU,
  output RegtoPC,
  output IMMtoPC,
  output ZerosToALU,
  output MemWrite,
  output MemtoReg,
  output Halt,
  output LED,
  output WriteLED,
  output MemRead,
  output PCtoReg
);

  wire Arith_LogDecoder_regwrite, JALDecoder_immtopc, JALDecoder_regwrite, MemDecoder_regwrite,
       PCDecoder_immtopc, ShifterDecoder_regwrite;
  wire [3:0] Arith_LogDecoder_aluoperation, PCDecoder_aluop;

  ShifterDecoder ShifterDecoder (
    .Opcode(Opcode), .ShiftSrc(ShiftSrc), .ShiftertoReg(ShifterToReg), .RegWrite(ShifterDecoder_regwrite));
  Arith_Log_Decoder Arith_LogDecoder (
    .Opcode(Opcode), .Subop(Subop), .ALUOperation(Arith_LogDecoder_aluoperation),
    .RegWrite(Arith_LogDecoder_regwrite), .ALUSrc(IMMtoALU));
  PCDecoder PCDecoder (
    .Opcode(Opcode), .Subop(Subop), .Zero(Zero), .Less(Less), .RegtoPC(RegtoPC), .IMMtoPC(PCDecoder_immtopc),
    .ZerosToALU(ZerosToALU), .ALUOp(PCDecoder_aluop));
  MemDecoder MemDecoder (
    .Opcode(Opcode), .Subop(Subop), .MemWrite(MemWrite), .MemtoReg(MemtoReg), .RegWrite(MemDecoder_regwrite),
    .MemRead(MemRead));
  HaltDecoder haltdecoder_1 (.Opcode(Opcode), .Halt(Halt), .LED(LED));
  PutDecoder PutDecoder (.Opcode(Opcode), .WriteLED(WriteLED));
  JALDecoder JALDecoder (
    .Opcode(Opcode), .IMMtoPC(JALDecoder_immtopc), .PCtoReg(PCtoReg), .RegWrite(JALDecoder_regwrite));
  or or_1 (RegWrite, ShifterDecoder_regwrite, Arith_LogDecoder_regwrite, MemDecoder_regwrite, JALDecoder_regwrite);
  or or_2 (IMMtoPC, PCDecoder_immtopc, JALDecoder_immtopc);
  assign ALUOp = Arith_LogDecoder_aluoperation | PCDecoder_aluop;  // OR_Gate or_3, 4 bits wide
endmodule

module MemDecoder (
  input  [3:0] Opcode,
  input  Subop,
  output MemWrite,
  output MemtoReg,
  output RegWrite,
  output MemRead
);

  and and_1 (MemWrite, ~Opcode[0], Opcode[1], Opcode[2], ~Opcode[3], Subop);  // AND_Gate
  and and_2 (MemRead, ~Opcode[0], Opcode[1], Opcode[2], ~Opcode[3], ~Subop);  // AND_Gate

  assign MemtoReg = MemRead;
  assign RegWrite = MemRead;
endmodule

module HaltDecoder (
  input  [3:0] Opcode,
  output Halt,
  output LED
);

  and and_1 (Halt, ~Opcode[3], Opcode[2], Opcode[1], Opcode[0]);  // AND_Gate

  assign LED = Halt;
endmodule

module PutDecoder (
  input  [3:0] Opcode,
  output WriteLED
);

  and and_1 (WriteLED, Opcode[0], Opcode[1], Opcode[2], Opcode[3]);
endmodule

module JALDecoder (
  input  [3:0] Opcode,
  output IMMtoPC,
  output PCtoReg,
  output RegWrite
);

  and and_1 (IMMtoPC, ~Opcode[0], ~Opcode[1], Opcode[2], Opcode[3]);  // AND_Gate

  assign PCtoReg = IMMtoPC;
  assign RegWrite = IMMtoPC;
endmodule

module ResultToLess (
  input  [15:0] Result,
  output Less
);


  assign Less = Result[15];
endmodule

module side (
  input  Op3,
  input  Op2,
  input  Op1,
  input  Op0,
  output Op3_2,
  output Op2_2,
  output Op1_2,
  output Op0_2
);

  wire not_1_out;

  and and_1 (Op1_2, Op3, not_1_out);
  not not_1 (not_1_out, Op2);

  assign Op0_2 = 1'b0;
  assign Op2_2 = 1'b0;
  assign Op3_2 = 1'b0;
endmodule

module IF_ID (
  input  clk,
  input  clr,
  input  [15:0] IF_inst,
  input  [7:0] IF_PC,
  input  En,
  output [15:0] ID_inst,
  output [7:0] ID_PC
);

  Register #(.width(16)) register_1 (.D(IF_inst), .en(En), .Q(ID_inst), .clk(clk), .clr(clr));
  Register register_2 (.D(IF_PC), .en(En), .Q(ID_PC), .clk(clk), .clr(clr));
endmodule

module ID_EX (
  input  Bubble_rst,
  input  clk,
  input  clr,
  input  ID_MemtoReg,
  input  [15:0] ID_imm,
  input  ID_RegWrite,
  input  [15:0] ID_R1,
  input  [2:0] ID_RegDst,
  input  ID_ALUSrc,
  input  [15:0] ID_R2,
  input  ID_MemRead,
  input  [7:0] Baddr,
  input  ID_MemWrite,
  input  [7:0] ID_PC,
  input  ID_Branch,
  input  [3:0] ID_ALUOp,
  input  ID_LED,
  input  ID_Zero,
  input  [2:0] Rs1,
  input  [2:0] Rs2,
  input  En,
  output EX_MemtoReg,
  output [15:0] EX_imm,
  output EX_RegWrite,
  output [15:0] EX_R1,
  output [2:0] EX_RegDst,
  output EX_ALUSrc,
  output [15:0] EX_R2,
  output EX_MemRead,
  output [7:0] Badder,
  output EX_MemWrite,
  output [7:0] EX_PC,
  output EX_Branch,
  output [3:0] EX_ALUOp,
  output EX_LED,
  output EX_Zero,
  output [2:0] EX_Rs1,
  output [2:0] EX_Rs2
);

  wire or_1_out;

  Register #(.width(16)) register_1 (.D(ID_imm), .en(En), .Q(EX_imm), .clk(clk), .clr(clr));
  Register #(.width(16)) register_2 (.D(ID_R1), .en(En), .Q(EX_R1), .clk(clk), .clr(clr));
  Register #(.width(16)) register_3 (.D(ID_R2), .en(En), .Q(EX_R2), .clk(clk), .clr(clr));
  Register register_4 (.D(Baddr), .en(En), .Q(Badder), .clk(clk), .clr(clr));
  Register register_5 (.D(ID_PC), .en(En), .Q(EX_PC), .clk(clk), .clr(clr));
  Register #(.width(1)) register_6 (.D(ID_MemtoReg), .en(En), .Q(EX_MemtoReg), .clk(clk), .clr(clr));
  Register #(.width(1)) register_7 (.D(ID_RegWrite), .en(En), .Q(EX_RegWrite), .clk(clk), .clr(or_1_out));
  Register #(.width(3)) register_8 (.D(ID_RegDst), .en(En), .Q(EX_RegDst), .clk(clk), .clr(clr));
  Register #(.width(1)) register_9 (.D(ID_ALUSrc), .en(En), .Q(EX_ALUSrc), .clk(clk), .clr(or_1_out));
  Register #(.width(1)) register_10 (.D(ID_MemRead), .en(En), .Q(EX_MemRead), .clk(clk), .clr(clr));
  Register #(.width(1)) register_11 (.D(ID_MemWrite), .en(En), .Q(EX_MemWrite), .clk(clk), .clr(clr));
  Register #(.width(1)) register_12 (.D(ID_Branch), .en(En), .Q(EX_Branch), .clk(clk), .clr(clr));
  Register #(.width(4)) register_13 (.D(ID_ALUOp), .en(En), .Q(EX_ALUOp), .clk(clk), .clr(or_1_out));
  Register #(.width(1)) register_14 (.D(ID_LED), .en(En), .Q(EX_LED), .clk(clk), .clr(clr));
  Register #(.width(1)) register_15 (.D(ID_Zero), .en(En), .Q(EX_Zero), .clk(clk), .clr(clr));
  Register #(.width(3)) register_16 (.D(Rs1), .en(En), .Q(EX_Rs1), .clk(clk), .clr(clr));
  Register #(.width(3)) register_17 (.D(Rs2), .en(En), .Q(EX_Rs2), .clk(clk), .clr(clr));
  or or_1 (or_1_out, clr, Bubble_rst);
endmodule

module EX_MEM (
  input  clk,
  input  clr,
  input  EX_MemtoReg,
  input  [15:0] EX_ALURes,
  input  EX_RegWrite,
  input  [15:0] EX_Wdata,
  input  EX_MemRead,
  input  EX_MemWrite,
  input  [7:0] Baddr,
  input  EX_PCSrc,
  input  [7:0] EX_PC,
  input  EX_Less,
  input  [15:0] EX_R1,
  input  [2:0] EX_RegDst,
  input  EX_LED,
  input  EX_Zero,
  input  En,
  output MEM_MemtoReg,
  output [15:0] MEM_ALURes,
  output MEM_RegWrite,
  output [15:0] MEM_Wdata,
  output MEM_MemRead,
  output MEM_MemWrite,
  output [7:0] Badder,
  output MEM_PCSrc,
  output [7:0] MEM_PC,
  output Mem_Less,
  output [15:0] MEM_R1,
  output [2:0] MEM_RegDst,
  output MEM_LED,
  output MEM_Zero
);

  Register #(.width(16)) register_1 (.D(EX_ALURes), .en(En), .Q(MEM_ALURes), .clk(clk), .clr(clr));
  Register #(.width(16)) register_2 (.D(EX_Wdata), .en(En), .Q(MEM_Wdata), .clk(clk), .clr(clr));
  Register register_3 (.D(Baddr), .en(En), .Q(Badder), .clk(clk), .clr(clr));
  Register register_4 (.D(EX_PC), .en(En), .Q(MEM_PC), .clk(clk), .clr(clr));
  Register #(.width(16)) register_5 (.D(EX_R1), .en(En), .Q(MEM_R1), .clk(clk), .clr(clr));
  Register #(.width(1)) register_6 (.D(EX_MemtoReg), .en(En), .Q(MEM_MemtoReg), .clk(clk), .clr(clr));
  Register #(.width(1)) register_7 (.D(EX_RegWrite), .en(En), .Q(MEM_RegWrite), .clk(clk), .clr(clr));
  Register #(.width(1)) register_8 (.D(EX_MemRead), .en(En), .Q(MEM_MemRead), .clk(clk), .clr(clr));
  Register #(.width(1)) register_9 (.D(EX_MemWrite), .en(En), .Q(MEM_MemWrite), .clk(clk), .clr(clr));
  Register #(.width(1)) register_10 (.D(EX_PCSrc), .en(En), .Q(MEM_PCSrc), .clk(clk), .clr(clr));
  Register #(.width(1)) register_11 (.D(EX_Less), .en(En), .Q(Mem_Less), .clk(clk), .clr(clr));
  Register #(.width(3)) register_12 (.D(EX_RegDst), .en(En), .Q(MEM_RegDst), .clk(clk), .clr(clr));
  Register #(.width(1)) register_13 (.D(EX_LED), .en(En), .Q(MEM_LED), .clk(clk), .clr(clr));
  Register #(.width(1)) register_14 (.D(EX_Zero), .en(En), .Q(MEM_Zero), .clk(clk), .clr(clr));
endmodule

module MEM_WB (
  input  clk,
  input  clr,
  input  MEM_MemtoReg,
  input  [15:0] MEM_ALURes,
  input  MEM_RegWrite,
  input  [15:0] MEM_Wdata,
  input  [2:0] MEM_RegDst,
  input  [7:0] MEM_PC,
  input  MEM_LED,
  input  En,
  output WB_MemtoReg,
  output [15:0] WB_ALURes,
  output WB_RegWrite,
  output [15:0] WB_Wdata,
  output [2:0] WB_RegDst,
  output [7:0] WB_PC,
  output WB_LED
);

  Register #(.width(16)) register_1 (.D(MEM_ALURes), .en(En), .Q(WB_ALURes), .clk(clk), .clr(clr));
  Register #(.width(16)) register_2 (.D(MEM_Wdata), .en(En), .Q(WB_Wdata), .clk(clk), .clr(clr));
  Register register_3 (.D(MEM_PC), .en(En), .Q(WB_PC), .clk(clk), .clr(clr));
  Register #(.width(1)) register_4 (.D(MEM_MemtoReg), .en(En), .Q(WB_MemtoReg), .clk(clk), .clr(clr));
  Register #(.width(1)) register_5 (.D(MEM_RegWrite), .en(En), .Q(WB_RegWrite), .clk(clk), .clr(clr));
  Register #(.width(3)) register_6 (.D(MEM_RegDst), .en(En), .Q(WB_RegDst), .clk(clk), .clr(clr));
  Register #(.width(1)) register_7 (.D(MEM_LED), .en(En), .Q(WB_LED), .clk(clk), .clr(clr));
endmodule

// PC
module main_temp (
  input  in_1
);

  wire ALU_zero, and_1_out, clk, Decoder_immtoalu, Decoder_immtopc, Decoder_led, Decoder_memwrite,
       Decoder_pctoreg, Decoder_regtopc, Decoder_shiftertoreg, Decoder_shiftsrc, Halt, Halt_EX, Halt_MEM,
       ImmtoALU, ImmtoALU_EX, ImmtoPC, ImmtoPC_EX, Instruction_Splitter_subop, Instruction_Splitter_unsigned,
       Less, Less_MEM, MemRead, MemRead_EX, MemRead_MEM, MemtoReg_EX, MemtoReg_in, MemtoReg_MEM, MemtoReg_WB,
       MemWrite, MemWrite_EX, MemWrite_MEM, not_1_out, PC_Src, PC_Src_MEM, ResultToLess_less, rst, Rwrite,
       Rwrite_EX, Rwrite_MEM, Rwrite_WB, undriven, undriven_2, undriven_6, undriven_7, undriven_8,
       undriven_9, Varun, WriteLED, WriteLED_EX, WriteLED_MEM, WriteLED_WB, ZerostoALU, ZerostoALU_EX,
       ZerostoALU_MEM;
  wire [2:0] Instruction_Splitter_readregister1, Instruction_Splitter_readregister2,
       Instruction_Splitter_writeregister, RegDst, RegDst_EX, RegDst_MEM, RegDst_WB;
  wire [3:0] ALUOp, ALUOp_EX, Decoder_aluop, Instruction_Splitter_opcode, Instruction_Splitter_shiftamount;
  wire [7:0] adder_1_out, Badder, Badder_EX, Badder_MEM, Instruction_Splitter_immediate, multiplexer_3_out,
       multiplexer_4_out, PC, PC_EX, PC_ID, PC_MEM, PC_WB, RegistertoAddress_2_address,
       RegistertoAddress_address;
  wire [15:0] ALU_result, ALURes, ALURes_MEM, ALURes_WB, bit_extender_1_out, imm, imm_EX, Instruc_in,
       Instruc_out, multiplexer_1_out, multiplexer_2_out, multiplexer_5_out, multiplexer_6_out,
       multiplexer_7_out, R1, R1_EX, R2, R2_EX, ram_1_data, register_1_q, Registers_readdata2,
       Shifter_shiftout, undriven_3, undriven_4, undriven_5, Wdata_MEM, Wdata_WB;

  IF_ID if_id_1 (
    .IF_inst(Instruc_in), .IF_PC(PC), .ID_inst(Instruc_out), .ID_PC(PC_ID), .clk(clk), .clr(rst),
    .En(and_1_out));
  not not_1 (not_1_out, undriven);
  Clock clock_1 (.out(clk));
  Register u_PC (.D(multiplexer_4_out), .en(not_1_out), .Q(PC), .clk(clk), .clr(rst));
  Button button_1 (.out(rst));
  and and_1 (and_1_out, in_1, Varun);
  Adder adder_1 (.a(PC), .b(8'h1), .out(adder_1_out));  // open: cin, cout
  ROM #(.dataWidth(16)) rom_1 (.addr(PC), .data(Instruc_in), .sel(1'b1));
  // ID_EX id_ex_1: pin names not known; wires that end beside it: MemtoReg_in, imm, Rwrite, R1, RegDst, ImmtoALU, R2, MemRead, Badder, MemWrite, PC_ID, ImmtoPC, ALUOp, Halt, WriteLED, ZerostoALU, clk, and_1_out, rst, MemtoReg_EX, imm_EX, Rwrite_EX, R1_EX, RegDst_EX, ImmtoALU_EX, R2_EX, MemRead_EX, Badder_EX, MemWrite_EX, PC_EX, ImmtoPC_EX, ALUOp_EX, Halt_EX, WriteLED_EX, ZerostoALU_EX
  InstructionSplitter Instruction_Splitter (
    .Instruction(Instruc_out), .Opcode(Instruction_Splitter_opcode),
    .ReadRegister1(Instruction_Splitter_readregister1), .ReadRegister2(Instruction_Splitter_readregister2),
    .WriteRegister(Instruction_Splitter_writeregister), .ShiftAmount(Instruction_Splitter_shiftamount),
    .SubOp(Instruction_Splitter_subop), .Unsigned(Instruction_Splitter_unsigned),
    .Immediate(Instruction_Splitter_immediate));
  SignExtend Sign_Extend (
    .Unsigned(Instruction_Splitter_unsigned), .Immediate(Instruction_Splitter_immediate),
    .SignExtendedImm(imm));
  ResultToLess ResultToLess (.Result(ALU_result), .Less(ResultToLess_less));
  RegisterFile Registers (
    .ReadRegister1(Instruction_Splitter_readregister1), .ReadRegister2(Instruction_Splitter_readregister2),
    .WriteRegister(Instruction_Splitter_writeregister), .WriteData(multiplexer_5_out),
    .WriteEnable(undriven_2), .Clock(clk), .ReadData1(R1), .ReadData2(Registers_readdata2));
  Decoder Decoder (
    .Opcode(Instruction_Splitter_opcode), .Subop(Instruction_Splitter_subop), .Zero(ALU_zero),
    .Less(ResultToLess_less), .ShiftSrc(Decoder_shiftsrc), .ShifterToReg(Decoder_shiftertoreg),
    .RegWrite(Rwrite), .ALUOp(Decoder_aluop), .IMMtoALU(Decoder_immtoalu), .RegtoPC(Decoder_regtopc),
    .IMMtoPC(Decoder_immtopc), .ZerosToALU(ZerostoALU), .MemWrite(Decoder_memwrite), .MemtoReg(MemtoReg_in),
    .Halt(Halt), .LED(Decoder_led), .WriteLED(WriteLED), .MemRead(MemRead), .PCtoReg(Decoder_pctoreg));
  Multiplexer #(.width(16), .disabled(0), .enable("false")) multiplexer_1 (
    .in0(Registers_readdata2), .in1(undriven_4), .out(multiplexer_1_out), .sel(Decoder_immtoalu));
  ALUtoPC RegistertoAddress (.ALUOut(undriven_5), .Address(RegistertoAddress_address));
  Multiplexer #(.width(16), .disabled(0), .enable("false")) multiplexer_2 (
    .in0(multiplexer_1_out), .in1({16{1'b0}}), .out(multiplexer_2_out), .sel(undriven_6));
  Multiplexer #(.width(8), .disabled(0), .enable("false")) multiplexer_3 (
    .in0(adder_1_out), .in1(Instruction_Splitter_immediate), .out(multiplexer_3_out), .sel(Decoder_immtopc));
  sixteen_bit_ALU ALU (
    .ALUOperation(Decoder_aluop), .a(undriven_5), .b(multiplexer_2_out), .Zero(ALU_zero), .Result(ALU_result));  // open: Overflow
  Multiplexer #(.width(8), .disabled(0), .enable("false")) multiplexer_4 (
    .in0(multiplexer_3_out), .in1(RegistertoAddress_address), .out(multiplexer_4_out), .sel(Decoder_regtopc));
  // EX_MEM ex_mem_1: pin names not known; wires that end beside it: MemtoReg_EX, ALURes, Rwrite_EX, R2_EX, MemRead_EX, MemWrite_EX, Badder_EX, PC_Src, PC_EX, Less, RegDst_EX, Halt_EX, WriteLED_EX, ZerostoALU_EX, clk, and_1_out, rst, MemtoReg_MEM, ALURes_MEM, Rwrite_MEM, Wdata_MEM, MemRead_MEM, MemWrite_MEM, Badder_MEM, PC_Src_MEM, PC_MEM, Less_MEM, RegDst_MEM, Halt_MEM, WriteLED_MEM, ZerostoALU_MEM
  ALUtoPC RegistertoAddress_2 (.ALUOut(Registers_readdata2), .Address(RegistertoAddress_2_address));
  Multiplexer #(.width(16), .disabled(0), .enable("false")) multiplexer_5 (
    .in0(multiplexer_6_out), .in1(bit_extender_1_out), .out(multiplexer_5_out), .sel(Decoder_pctoreg));
  Shifter Shifter (
    .Subop(Instruction_Splitter_subop), .Data(undriven_3), .ShamtReg(Registers_readdata2),
    .ShiftSrc(Decoder_shiftsrc), .Shamt(Instruction_Splitter_shiftamount), .ShiftOut(Shifter_shiftout));
  assign bit_extender_1_out = {{8{1'b0}}, adder_1_out};  // Bit_Extender bit_extender_1
  Multiplexer #(.width(16), .disabled(0), .enable("false")) multiplexer_6 (
    .in0(multiplexer_7_out), .in1(Shifter_shiftout), .out(multiplexer_6_out), .sel(Decoder_shiftertoreg));
  RAM #(.dataWidth(16), .bus("separate")) ram_1 (
    .addr(RegistertoAddress_2_address), .din(undriven_3), .data(ram_1_data), .str(Decoder_memwrite),
    .sel(1'b1), .clk(clk), .ld(undriven_7));  // open: clr
  Multiplexer #(.width(16), .disabled(0), .enable("false")) multiplexer_7 (
    .in0(ALU_result), .in1(ram_1_data), .out(multiplexer_7_out), .sel(undriven_9));
  Hex_Digit_Display hex_digit_display_1 (.value(register_1_q[15:12]));  // open: dp
  Register #(.width(16)) register_1 (.D(undriven_3), .en(undriven_8), .Q(register_1_q), .clk(clk));  // open: clr
  LED u_Halt (.in(Decoder_led));
  Hex_Digit_Display hex_digit_display_2 (.value(register_1_q[11:8]));  // open: dp
  Hex_Digit_Display hex_digit_display_3 (.value(register_1_q[7:4]));  // open: dp
  Hex_Digit_Display hex_digit_display_4 (.value(register_1_q[3:0]));  // open: dp
  MEM_WB mem_wb_1 (
    .MEM_MemtoReg(MemtoReg_MEM), .MEM_ALURes(ALURes_MEM), .MEM_RegWrite(Rwrite_MEM), .MEM_Wdata(Wdata_MEM),
    .MEM_RegDst(RegDst_MEM), .MEM_PC(PC_MEM), .MEM_LED(WriteLED_MEM), .WB_MemtoReg(MemtoReg_WB),
    .WB_ALURes(ALURes_WB), .WB_RegWrite(Rwrite_WB), .WB_Wdata(Wdata_WB), .WB_RegDst(RegDst_WB),
    .WB_PC(PC_WB), .WB_LED(WriteLED_WB), .clk(clk), .clr(rst), .En(and_1_out));

  // Notes on the sheet:
  //   IF/ID
  //   for stall states
  //   contents of rom_1 (hex, n*v repeats v):
  //   1 1104 241 1303 40 f000 241 1300 481 1503 281 6c1 1705 2c1 f200 901 1900 18ff f800 b41 1bf0 1b0f
  //   fa00 d81 1d19 fc1 1f20 3dc0 fc00 1 11e0 241 1378 3041 f000 481 150d 6c1 1708 44c0 f400 901 1910 b41
  //   1b04 4941 f800 d81 1d02 5c02 fc00 fc1 1f10 5e03 fe00 1 1140 61c1 63c0 f200 481 15ff 6c1 1701 845b
  //   865b 901 1900 985f b41 1b00 d81 1d00 1ce9 aa63 ac63 fc1 1f00 1 1119 be67 b067 e054 7000 c259 6c1
  //   170a f600 7000 d200 7000 fc1 1f01 fe00 7000 fc1 1f02 fe00 7000 fc1 1f03 fe00 7000 fc1 1f04 fe00 7000
  //   ID/EX
  //   EX/MEM
  //   MEM/WB
endmodule

module CPU (
  input  in_1
);

  wire alu_zero, and_1_out, and_2_out, and_3_out, Bubble, clk, comparator_1_eq, Decoder_led, Decoder_pctoreg,
       Decoder_shiftertoreg, Decoder_shiftsrc, Halt, ImmtoALU, ImmtoALU_EX, ImmtoPC, ImmtoPC_EX,
       Instruction_Splitter_subop, Instruction_Splitter_unsigned, Less, Less_MEM, MemRead, MemRead_EX,
       MemRead_MEM, MemtoReg_EX, MemtoReg_in, MemtoReg_MEM, MemtoReg_WB, MemWrite, MemWrite_EX, MemWrite_MEM,
       not_1_out, not_2_out, not_3_out, not_4_out, or_1_out, PC_Src, PC_Src_MEM, PC_Write, register_1_q,
       RegtoPC, rst, Rwrite, Rwrite_EX, Rwrite_MEM, Rwrite_WB, W_en, WriteLED, WriteLED_EX, WriteLED_MEM,
       WriteLED_WB, ZerostoALU, ZerostoALU_EX, ZerostoALU_MEM;
  wire [1:0] ALU_A_sel, ALU_B_sel;
  wire [2:0] RDst, RegDst, RegDst_EX, RegDst_MEM, RegDst_WB, Rs1, Rs1_EX, Rs2, Rs2_EX;
  wire [3:0] ALUOp, ALUOp_EX, Instruction_Splitter_opcode, Instruction_Splitter_shiftamount;
  wire [7:0] adder_1_out, Badder, Badder_EX, Badder_MEM, Instruction_Splitter_immediate, multiplexer_1_out,
       multiplexer_2_out, PC, PC_EX, PC_ID, PC_MEM, PC_WB, RegistertoAddress_2_address,
       RegistertoAddress_address;
  wire [15:0] ALU_bot, ALU_top, ALURes, ALURes_MEM, ALURes_WB, bit_extender_1_out, EX_MEM_Instruction_2_q,
       EX_MEM_Instruction_q, ID_EX_Instruction_q, IF_ID_Instruction_q, imm, imm_EX, Instruc_in, Instruc_out,
       multiplexer_3_out, multiplexer_4_out, multiplexer_6_out, multiplexer_7_out, multiplexer_10_out, R1,
       R1_EX, R1_MEM, R2, R2_EX, ram_1_data, register_2_q, Shifter_shiftout, Wdata_MEM, Wdata_WB;

  Clock clock_1 (.out(clk));
  IF_ID if_id_1 (
    .IF_inst(Instruc_in), .IF_PC(PC), .ID_inst(Instruc_out), .ID_PC(PC_ID), .clk(clk), .clr(rst),
    .En(and_1_out));
  and and_1 (and_1_out, not_3_out, not_1_out);
  not not_1 (not_1_out, Halt);
  HazardDetectionUnit hazarddetectionunit_1 (
    .ID_EX_MemRead(MemRead), .IF_ID_Rs1(Rs1), .ID_EX_Rd(RegDst), .IF_ID_Rs2(Rs2), .PCWrite(PC_Write),
    .IF_IF_Write(Rwrite), .Bubble(Bubble));
  and and_2 (and_2_out, PC_Write, not_2_out);
  not not_2 (not_2_out, Halt);
  Register #(.width(1), .trigger("falling")) register_1 (.D(Bubble), .en(1'b1), .Q(register_1_q), .clk(clk), .clr(rst));
  or or_1 (or_1_out, rst, register_1_q);
  Register #(.width(16)) IF_ID_Instruction (
    .D(Instruc_in), .en(not_3_out), .Q(IF_ID_Instruction_q), .clk(clk));  // open: clr
  Register u_PC (.D(multiplexer_2_out), .en(and_2_out), .Q(PC), .clk(clk), .clr(rst));
  Button button_1 (.out(rst));
  Register #(.width(16)) ID_EX_Instruction (
    .D(IF_ID_Instruction_q), .en(not_3_out), .Q(ID_EX_Instruction_q), .clk(clk));  // open: clr
  Adder adder_1 (.a(PC), .b(8'h1), .out(adder_1_out));  // open: cin, cout
  ROM #(.dataWidth(16)) rom_1 (.addr(PC), .data(Instruc_in), .sel(1'b1));
  ID_EX id_ex_1 (
    .ID_MemtoReg(MemtoReg_in), .ID_imm(imm), .ID_RegWrite(Rwrite), .ID_R1(R1), .ID_RegDst(RegDst),
    .ID_ALUSrc(ImmtoALU), .ID_R2(R2), .ID_MemRead(MemRead), .Baddr(Badder), .ID_MemWrite(MemWrite),
    .ID_PC(PC_ID), .ID_Branch(ImmtoPC), .ID_ALUOp(ALUOp), .ID_LED(WriteLED), .ID_Zero(ZerostoALU),
    .EX_MemtoReg(MemtoReg_EX), .EX_imm(imm_EX), .EX_RegWrite(Rwrite_EX), .EX_R1(R1_EX),
    .EX_RegDst(RegDst_EX), .EX_ALUSrc(ImmtoALU_EX), .EX_R2(R2_EX), .EX_MemRead(MemRead_EX),
    .Badder(Badder_EX), .EX_MemWrite(MemWrite_EX), .EX_PC(PC_EX), .EX_Branch(ImmtoPC_EX),
    .EX_ALUOp(ALUOp_EX), .EX_LED(WriteLED_EX), .EX_Zero(ZerostoALU_EX), .clk(clk), .clr(rst), .En(not_3_out),
    .Rs1(Rs1), .EX_Rs1(Rs1_EX), .Rs2(Rs2), .EX_Rs2(Rs2_EX), .Bubble_rst(or_1_out));
  Register #(.width(16)) EX_MEM_Instruction (
    .D(ID_EX_Instruction_q), .en(not_3_out), .Q(EX_MEM_Instruction_q), .clk(clk));  // open: clr
  forwarding_unit forwarding_unit_1 (
    .EX_MEM_RegWrite(Rwrite_MEM), .ID_EX_Rs1(Rs1_EX), .EX_MEM_Rd(RegDst_MEM), .ID_EX_Rs2(Rs2_EX),
    .MEM_WB_RegWrite(Rwrite_WB), .MEM_WB_Rd(RegDst_WB), .AluMuxA(ALU_A_sel), .AluMuxB(ALU_B_sel));
  SignExtend Sign_Extend (
    .Unsigned(Instruction_Splitter_unsigned), .Immediate(Instruction_Splitter_immediate),
    .SignExtendedImm(imm));
  InstructionSplitter Instruction_Splitter (
    .Instruction(Instruc_out), .Opcode(Instruction_Splitter_opcode), .ReadRegister1(Rs1),
    .ReadRegister2(Rs2), .WriteRegister(RegDst), .ShiftAmount(Instruction_Splitter_shiftamount),
    .SubOp(Instruction_Splitter_subop), .Unsigned(Instruction_Splitter_unsigned),
    .Immediate(Instruction_Splitter_immediate));
  ResultToLess resulttoless_1 (.Result(ALURes_MEM), .Less(Less));
  Register #(.width(16)) EX_MEM_Instruction_2 (
    .D(EX_MEM_Instruction_q), .en(not_3_out), .Q(EX_MEM_Instruction_2_q), .clk(clk));  // open: clr
  // Probe on RDst
  // Probe on multiplexer_3_out
  Decoder Decoder (
    .Opcode(Instruction_Splitter_opcode), .Subop(Instruction_Splitter_subop), .Zero(alu_zero),
    .Less(Less_MEM), .ShiftSrc(Decoder_shiftsrc), .ShifterToReg(Decoder_shiftertoreg), .RegWrite(Rwrite),
    .ALUOp(ALUOp), .IMMtoALU(ImmtoALU), .RegtoPC(RegtoPC), .IMMtoPC(ImmtoPC), .ZerosToALU(ZerostoALU),
    .MemWrite(MemWrite), .MemtoReg(MemtoReg_in), .Halt(Halt), .LED(Decoder_led), .WriteLED(WriteLED),
    .MemRead(MemRead), .PCtoReg(Decoder_pctoreg));
  RegisterFile Registers (
    .ReadRegister1(Rs1), .ReadRegister2(Rs2), .WriteRegister(RDst), .WriteData(multiplexer_3_out),
    .WriteEnable(W_en), .Clock(clk), .ReadData1(R1), .ReadData2(R2));
  Register #(.width(16)) MEM_WB_Instruction (.D(EX_MEM_Instruction_2_q), .en(not_3_out), .clk(clk));  // open: Q, clr
  ALUtoPC RegistertoAddress (.ALUOut(R1), .Address(RegistertoAddress_address));
  Multiplexer #(.width(8), .disabled(0), .enable("false")) multiplexer_1 (
    .in0(adder_1_out), .in1(Instruction_Splitter_immediate), .out(multiplexer_1_out), .sel(ImmtoPC_EX));
  Multiplexer #(.width(8), .disabled(0), .enable("false")) multiplexer_2 (
    .in0(multiplexer_1_out), .in1(RegistertoAddress_address), .out(multiplexer_2_out), .sel(RegtoPC));
  EX_MEM ex_mem_1 (
    .EX_MemtoReg(MemtoReg_EX), .EX_ALURes(ALURes), .EX_RegWrite(Rwrite_EX), .EX_Wdata(R2_EX),
    .EX_MemRead(MemRead_EX), .EX_MemWrite(MemWrite_EX), .Baddr(Badder_EX), .EX_PCSrc(PC_Src), .EX_PC(PC_EX),
    .EX_Less(Less), .EX_LED(WriteLED_EX), .EX_Zero(ZerostoALU_EX), .MEM_MemtoReg(MemtoReg_MEM),
    .MEM_ALURes(ALURes_MEM), .MEM_RegWrite(Rwrite_MEM), .MEM_Wdata(Wdata_MEM), .MEM_MemRead(MemRead_MEM),
    .MEM_MemWrite(MemWrite_MEM), .Badder(Badder_MEM), .MEM_PCSrc(PC_Src_MEM), .MEM_PC(PC_MEM),
    .Mem_Less(Less_MEM), .MEM_RegDst(RegDst_MEM), .MEM_LED(WriteLED_MEM), .MEM_Zero(ZerostoALU_MEM),
    .clk(clk), .clr(rst), .En(not_3_out), .EX_RegDst(RegDst_EX), .MEM_R1(R1_MEM), .EX_R1(R1_EX));
  not not_3 (not_3_out, in_1);
  sixteen_bit_ALU ALU (
    .ALUOperation(ALUOp_EX), .a(ALU_top), .b(ALU_bot), .Zero(alu_zero), .Result(ALURes));  // open: Overflow
  Multiplexer #(.width(16), .disabled(0), .enable("false")) multiplexer_3 (
    .in0(multiplexer_4_out), .in1(bit_extender_1_out), .out(multiplexer_3_out), .sel(Decoder_pctoreg));
  Shifter Shifter (
    .Subop(Instruction_Splitter_subop), .Data(R1_EX), .ShamtReg(R2), .ShiftSrc(Decoder_shiftsrc),
    .Shamt(Instruction_Splitter_shiftamount), .ShiftOut(Shifter_shiftout));
  assign bit_extender_1_out = {{8{1'b0}}, adder_1_out};  // Bit_Extender bit_extender_1
  LED u_Halt (.in(Decoder_led));
  // Probe on ALURes
  Multiplexer #(.width(16), .disabled(0), .enable("false")) multiplexer_4 (
    .in0(multiplexer_7_out), .in1(Shifter_shiftout), .out(multiplexer_4_out), .sel(Decoder_shiftertoreg));
  // Probe on ALURes_MEM
  // Probe on RegistertoAddress_2_address
  ALUtoPC RegistertoAddress_2 (.ALUOut(ALURes_MEM), .Address(RegistertoAddress_2_address));
  // Probe on R1_MEM
  // Probe on R1_MEM
  Register #(.width(16)) register_2 (.D(R1_MEM), .en(WriteLED_MEM), .Q(register_2_q), .clk(clk), .clr(rst));
  RAM #(.dataWidth(16), .bus("separate")) ram_1 (
    .addr(RegistertoAddress_2_address), .din(R1_MEM), .data(ram_1_data), .str(MemWrite_MEM), .sel(1'b1),
    .clk(clk), .ld(MemRead_MEM), .clr(rst));
  Hex_Digit_Display hex_digit_display_1 (.value(register_2_q[15:12]));  // open: dp
  Hex_Digit_Display hex_digit_display_2 (.value(register_2_q[11:8]));  // open: dp
  Hex_Digit_Display hex_digit_display_3 (.value(register_2_q[7:4]));  // open: dp
  Hex_Digit_Display hex_digit_display_4 (.value(register_2_q[3:0]));  // open: dp
  Multiplexer #(.select(2), .width(16), .enable("false")) multiplexer_5 (
    .in0(R1_EX), .in1(ALURes_WB), .in2(ALURes_MEM), .out(ALU_top), .sel(ALU_A_sel));  // open: in3
  Multiplexer #(.select(2), .width(16), .enable("false")) multiplexer_6 (
    .in0(R2_EX), .in1(ALURes_WB), .in2(ALURes_MEM), .out(multiplexer_6_out), .sel(ALU_B_sel));  // open: in3
  MEM_WB mem_wb_1 (
    .MEM_MemtoReg(MemtoReg_MEM), .MEM_ALURes(ALURes_MEM), .MEM_RegWrite(Rwrite_MEM), .MEM_Wdata(Wdata_MEM),
    .MEM_RegDst(RegDst_MEM), .MEM_PC(PC_MEM), .MEM_LED(WriteLED_MEM), .WB_MemtoReg(MemtoReg_WB),
    .WB_ALURes(ALURes_WB), .WB_RegWrite(Rwrite_WB), .WB_Wdata(Wdata_WB), .WB_RegDst(RegDst_WB),
    .WB_PC(PC_WB), .WB_LED(WriteLED_WB), .clk(clk), .clr(rst), .En(not_3_out));
  Multiplexer #(.width(16), .disabled(0), .enable("false")) multiplexer_7 (
    .in0(ALURes_WB), .in1(ram_1_data), .out(multiplexer_7_out), .sel(MemtoReg_MEM));
  Comparator #(.width(1)) comparator_1 (.a(1'b1), .b(MemtoReg_MEM), .eq(comparator_1_eq));  // open: gt, lt
  Multiplexer #(.width(3), .enable("false")) multiplexer_8 (
    .in0(RegDst_WB), .in1(RegDst_MEM), .out(RDst), .sel(comparator_1_eq));
  and and_3 (and_3_out, Rwrite_WB, not_4_out);
  Multiplexer #(.enable("false")) multiplexer_9 (.in0(and_3_out), .in1(1'b1), .out(W_en), .sel(comparator_1_eq));
  Multiplexer #(.width(16), .disabled(0), .enable("false")) multiplexer_10 (
    .in0(multiplexer_6_out), .in1(imm_EX), .out(multiplexer_10_out), .sel(ImmtoALU_EX));
  not not_4 (not_4_out, WriteLED_WB);
  Multiplexer #(.width(16), .disabled(0), .enable("false")) multiplexer_11 (
    .in0(multiplexer_10_out), .in1({16{1'b0}}), .out(ALU_bot), .sel(ZerostoALU_EX));

  // Notes on the sheet:
  //   IF/ID
  //   Hazard Unit
  //   Forwarding Unit
  //   contents of rom_1 (hex, n*v repeats v):
  //   16f6 1914 1206 1afe 1d03 8c0 22c0 b80 f600 f200 f800 fa00 7000
  //   ID/EX
  //   EX/MEM
  //   ALU_top
  //   ALU_bot
  //   MEM/WB
endmodule

module HazardDetectionUnit (
  input  ID_EX_MemRead,
  input  [2:0] IF_ID_Rs1,
  input  [2:0] ID_EX_Rd,
  input  [2:0] IF_ID_Rs2,
  output PCWrite,
  output IF_IF_Write,
  output Bubble
);

  wire comparator_1_eq, comparator_2_eq, or_1_out;

  Comparator #(.width(3)) comparator_1 (.a(IF_ID_Rs1), .b(ID_EX_Rd), .eq(comparator_1_eq));  // open: gt, lt
  Comparator #(.width(3)) comparator_2 (.a(ID_EX_Rd), .b(IF_ID_Rs2), .eq(comparator_2_eq));  // open: gt, lt
  or or_1 (or_1_out, comparator_1_eq, comparator_2_eq);
  and and_1 (Bubble, ID_EX_MemRead, or_1_out);
  not not_1 (IF_IF_Write, Bubble);

  assign PCWrite = IF_IF_Write;
endmodule

module forwarding_unit (
  input  EX_MEM_RegWrite,
  input  [2:0] ID_EX_Rs1,
  input  [2:0] EX_MEM_Rd,
  input  [2:0] ID_EX_Rs2,
  input  MEM_WB_RegWrite,
  input  [2:0] MEM_WB_Rd,
  output [1:0] AluMuxA,
  output [1:0] AluMuxB
);

  wire comparator_1_eq, comparator_2_eq, comparator_3_eq, comparator_4_eq;
  wire [1:0] and_3_out, and_4_out;

  Comparator #(.width(3)) comparator_1 (.a(ID_EX_Rs1), .b(MEM_WB_Rd), .eq(comparator_1_eq));  // open: gt, lt
  Comparator #(.width(3)) comparator_2 (.a(MEM_WB_Rd), .b(ID_EX_Rs2), .eq(comparator_2_eq));  // open: gt, lt
  Comparator #(.width(3)) comparator_3 (.a(ID_EX_Rs1), .b(EX_MEM_Rd), .eq(comparator_3_eq));  // open: gt, lt
  Comparator #(.width(3)) comparator_4 (.a(EX_MEM_Rd), .b(ID_EX_Rs2), .eq(comparator_4_eq));  // open: gt, lt
  and and_1 (and_3_out[1], EX_MEM_RegWrite, comparator_3_eq);
  and and_2 (and_4_out[1], EX_MEM_RegWrite, comparator_4_eq);
  and and_3 (and_3_out[0], MEM_WB_RegWrite, comparator_1_eq, ~and_3_out[1]);  // AND_Gate
  and and_4 (and_4_out[0], MEM_WB_RegWrite, comparator_2_eq, and_4_out[1]);
  Multiplexer #(.select(2), .width(2), .enable("false")) multiplexer_1 (
    .in0(2'b00), .in1(2'b01), .in2(2'b10), .out(AluMuxA), .sel(and_3_out));  // open: in3
  Multiplexer #(.select(2), .width(2), .enable("false")) multiplexer_2 (
    .in0(2'b00), .in1(2'b01), .in2(2'b10), .out(AluMuxB), .sel(and_4_out));  // open: in3

  // Notes on the sheet:
  //   10
  //   10
  //   01
  //   01
endmodule
