// Logisim project NEWWWW fallingedge.circ as structural Verilog
module main (
);

  wire ALU_zero, button_1_out, clock_1_out, Decoder_halt, Decoder_immtoalu, Decoder_immtopc, Decoder_led,
       Decoder_memread, Decoder_memtoreg, Decoder_memwrite, Decoder_pctoreg, Decoder_regtopc,
       Decoder_regwrite, Decoder_shiftertoreg, Decoder_shiftsrc, Decoder_writeled, Decoder_zerostoalu,
       Instruction_Splitter_subop, Instruction_Splitter_unsigned, not_1_out, ResultToLess_less;
  wire [2:0] Instruction_Splitter_readregister1, Instruction_Splitter_readregister2,
       Instruction_Splitter_writeregister;
  wire [3:0] Decoder_aluop, Instruction_Splitter_opcode, Instruction_Splitter_shiftamount;
  wire [7:0] adder_1_out, Instruction_Splitter_immediate, multiplexer_3_out, multiplexer_4_out, PC_q,
       RegistertoAddress_2_address, RegistertoAddress_address;
  wire [15:0] ALU_result, bit_extender_1_out, multiplexer_1_out, multiplexer_2_out, multiplexer_5_out,
       multiplexer_6_out, multiplexer_7_out, ram_1_data, register_1_q, Registers_readdata1,
       Registers_readdata2, rom_1_data, Shifter_shiftout, Sign_Extend_signextendedimm;

  not not_1 (not_1_out, Decoder_halt);
  Clock clock_1 (.out(clock_1_out));
  Register PC (.D(multiplexer_4_out), .en(not_1_out), .Q(PC_q), .clk(clock_1_out), .clr(button_1_out));
  Button button_1 (.out(button_1_out));
  Adder adder_1 (.a(PC_q), .b(8'h1), .out(adder_1_out));  // open: cin, cout
  ROM #(.dataWidth(16)) rom_1 (.addr(PC_q), .data(rom_1_data), .sel(1'b1));
  InstructionSplitter Instruction_Splitter (
    .Instruction(rom_1_data), .Opcode(Instruction_Splitter_opcode),
    .ReadRegister1(Instruction_Splitter_readregister1), .ReadRegister2(Instruction_Splitter_readregister2),
    .WriteRegister(Instruction_Splitter_writeregister), .ShiftAmount(Instruction_Splitter_shiftamount),
    .SubOp(Instruction_Splitter_subop), .Unsigned(Instruction_Splitter_unsigned),
    .Immediate(Instruction_Splitter_immediate));
  SignExtend Sign_Extend (
    .Unsigned(Instruction_Splitter_unsigned), .Immediate(Instruction_Splitter_immediate),
    .SignExtendedImm(Sign_Extend_signextendedimm));
  ResultToLess ResultToLess (.Result(ALU_result), .Less(ResultToLess_less));
  RegisterFile Registers (
    .ReadRegister1(Instruction_Splitter_readregister1), .ReadRegister2(Instruction_Splitter_readregister2),
    .WriteRegister(Instruction_Splitter_writeregister), .WriteData(multiplexer_5_out),
    .WriteEnable(Decoder_regwrite), .Clock(clock_1_out), .ReadData1(Registers_readdata1),
    .ReadData2(Registers_readdata2));
  Decoder Decoder (
    .Opcode(Instruction_Splitter_opcode), .Subop(Instruction_Splitter_subop), .Zero(ALU_zero),
    .Less(ResultToLess_less), .ShiftSrc(Decoder_shiftsrc), .ShifterToReg(Decoder_shiftertoreg),
    .RegWrite(Decoder_regwrite), .ALUOp(Decoder_aluop), .IMMtoALU(Decoder_immtoalu),
    .RegtoPC(Decoder_regtopc), .IMMtoPC(Decoder_immtopc), .ZerosToALU(Decoder_zerostoalu),
    .MemWrite(Decoder_memwrite), .MemtoReg(Decoder_memtoreg), .Halt(Decoder_halt), .LED(Decoder_led),
    .WriteLED(Decoder_writeled), .MemRead(Decoder_memread), .PCtoReg(Decoder_pctoreg));
  Multiplexer #(.width(16), .disabled(0), .enable("false")) multiplexer_1 (
    .in0(Registers_readdata2), .in1(Sign_Extend_signextendedimm), .out(multiplexer_1_out),
    .sel(Decoder_immtoalu));
  ALUtoPC RegistertoAddress (.ALUOut(Registers_readdata1), .Address(RegistertoAddress_address));
  Multiplexer #(.width(16), .disabled(0), .enable("false")) multiplexer_2 (
    .in0(multiplexer_1_out), .in1({16{1'b0}}), .out(multiplexer_2_out), .sel(Decoder_zerostoalu));
  Multiplexer #(.width(8), .disabled(0), .enable("false")) multiplexer_3 (
    .in0(adder_1_out), .in1(Instruction_Splitter_immediate), .out(multiplexer_3_out), .sel(Decoder_immtopc));
  sixteen_bit_ALU ALU (
    .ALUOperation(Decoder_aluop), .a(Registers_readdata1), .b(multiplexer_2_out), .Zero(ALU_zero),
    .Result(ALU_result));  // open: Overflow
  Multiplexer #(.width(8), .disabled(0), .enable("false")) multiplexer_4 (
    .in0(multiplexer_3_out), .in1(RegistertoAddress_address), .out(multiplexer_4_out), .sel(Decoder_regtopc));
  ALUtoPC RegistertoAddress_2 (.ALUOut(Registers_readdata2), .Address(RegistertoAddress_2_address));
  Multiplexer #(.width(16), .disabled(0), .enable("false")) multiplexer_5 (
    .in0(multiplexer_6_out), .in1(bit_extender_1_out), .out(multiplexer_5_out), .sel(Decoder_pctoreg));
  Shifter Shifter (
    .Subop(Instruction_Splitter_subop), .Data(Registers_readdata1), .ShamtReg(Registers_readdata2),
    .ShiftSrc(Decoder_shiftsrc), .Shamt(Instruction_Splitter_shiftamount), .ShiftOut(Shifter_shiftout));
  assign bit_extender_1_out = {{8{1'b0}}, adder_1_out};  // Bit_Extender bit_extender_1
  Multiplexer #(.width(16), .disabled(0), .enable("false")) multiplexer_6 (
    .in0(multiplexer_7_out), .in1(Shifter_shiftout), .out(multiplexer_6_out), .sel(Decoder_shiftertoreg));
  RAM #(.dataWidth(16), .bus("separate")) ram_1 (
    .addr(RegistertoAddress_2_address), .din(Registers_readdata1), .data(ram_1_data), .str(Decoder_memwrite),
    .sel(1'b1), .clk(clock_1_out), .ld(Decoder_memread));  // open: clr
  Multiplexer #(.width(16), .disabled(0), .enable("false")) multiplexer_7 (
    .in0(ALU_result), .in1(ram_1_data), .out(multiplexer_7_out), .sel(Decoder_memtoreg));
  Hex_Digit_Display hex_digit_display_1 (.value(register_1_q[15:12]));  // open: dp
  Register #(.width(16)) register_1 (
    .D(Registers_readdata1), .en(Decoder_writeled), .Q(register_1_q), .clk(clock_1_out));  // open: clr
  LED Halt (.in(Decoder_led));
  Hex_Digit_Display hex_digit_display_2 (.value(register_1_q[7:4]));  // open: dp
  Hex_Digit_Display hex_digit_display_3 (.value(register_1_q[11:8]));  // open: dp
  Hex_Digit_Display hex_digit_display_4 (.value(register_1_q[3:0]));  // open: dp

  // Notes on the sheet:
  //   contents of rom_1 (hex, n*v repeats v):
  //   16f6 1914 1206 1afe 1d03 8c0 22c0 b80 f600 f200 f800 fa00 7000
endmodule

module InstructionSplitter (
  input  [15:0] Instruction,
  output [3:0] Opcode,
  output [2:0] ReadRegister1,
  output [2:0] ReadRegister2,
  output [2:0] WriteRegister,
  output [3:0] ShiftAmount,
  output SubOp,
  output Unsigned,
  output [7:0] Immediate
);


  assign Immediate = Instruction[7:0];
  assign Opcode = Instruction[15:12];
  assign ReadRegister1 = Instruction[11:9];
  assign ReadRegister2 = Instruction[8:6];
  assign ShiftAmount = Instruction[4:1];
  assign SubOp = Instruction[0];
  assign Unsigned = Instruction[8];
  assign WriteRegister = Instruction[11:9];
endmodule

module SignExtend (
  input  Unsigned,
  input  [7:0] Immediate,
  output [15:0] SignExtendedImm
);

  wire [15:0] bit_extender_1_out, bit_extender_2_out;

  assign bit_extender_1_out = {{8{Immediate[7]}}, Immediate};  // Bit_Extender bit_extender_1
  assign bit_extender_2_out = {{8{1'b0}}, Immediate};  // Bit_Extender bit_extender_2
  Multiplexer #(.width(16), .disabled(0), .enable("false")) multiplexer_1 (
    .in0(bit_extender_1_out), .in1(bit_extender_2_out), .out(SignExtendedImm), .sel(Unsigned));
endmodule

module ALUtoPC (
  input  [15:0] ALUOut,
  output [7:0] Address
);


  assign Address = ALUOut[7:0];
endmodule

module Shifter (
  input  Subop,
  input  [15:0] Data,
  input  [15:0] ShamtReg,
  input  ShiftSrc,
  input  [3:0] Shamt,
  output [15:0] ShiftOut
);

  wire [3:0] multiplexer_1_out;
  wire [15:0] shifter_1_out, shifter_2_out;

  Multiplexer #(.width(4), .disabled(0), .enable("false")) multiplexer_1 (
    .in0(ShamtReg[3:0]), .in1(Shamt), .out(multiplexer_1_out), .sel(ShiftSrc));
  Shifter_part #(.width(16)) shifter_1 (.in(Data), .\dist (multiplexer_1_out), .out(shifter_1_out));
  Shifter_part #(.width(16), .shift("lr")) shifter_2 (.in(Data), .\dist (multiplexer_1_out), .out(shifter_2_out));
  Multiplexer #(.width(16), .disabled(0), .enable("false")) multiplexer_2 (
    .in0(shifter_1_out), .in1(shifter_2_out), .out(ShiftOut), .sel(Subop));
endmodule

module RegisterFile (
  input  [2:0] ReadRegister1,
  input  [2:0] ReadRegister2,
  input  [2:0] WriteRegister,
  input  [15:0] WriteData,
  input  WriteEnable,
  input  Clock,
  output [15:0] ReadData1,
  output [15:0] ReadData2
);

  wire decoder_1_out0, decoder_1_out1, decoder_1_out2, decoder_1_out3, decoder_1_out4, decoder_1_out5,
       decoder_1_out6, decoder_1_out7;
  wire [15:0] register_1_q, register_2_q, register_3_q, register_4_q, register_5_q, register_6_q,
       register_7_q, register_8_q;

  Decoder_part #(.select(3), .disabled(0)) decoder_1 (
    .out0(decoder_1_out0), .out1(decoder_1_out1), .out2(decoder_1_out2), .out3(decoder_1_out3),
    .out4(decoder_1_out4), .out5(decoder_1_out5), .out6(decoder_1_out6), .out7(decoder_1_out7),
    .sel(WriteRegister), .en(WriteEnable));
  Register #(.width(16)) register_1 (.D(WriteData), .en(decoder_1_out0), .Q(register_1_q), .clk(Clock));  // open: clr
  Register #(.width(16)) register_2 (.D(WriteData), .en(decoder_1_out1), .Q(register_2_q), .clk(Clock));  // open: clr
  Register #(.width(16)) register_3 (.D(WriteData), .en(decoder_1_out2), .Q(register_3_q), .clk(Clock));  // open: clr
  Register #(.width(16)) register_4 (.D(WriteData), .en(decoder_1_out3), .Q(register_4_q), .clk(Clock));  // open: clr
  Register #(.width(16)) register_5 (.D(WriteData), .en(decoder_1_out4), .Q(register_5_q), .clk(Clock));  // open: clr
  Register #(.width(16)) register_6 (.D(WriteData), .en(decoder_1_out5), .Q(register_6_q), .clk(Clock));  // open: clr
  Register #(.width(16)) register_7 (.D(WriteData), .en(decoder_1_out6), .Q(register_7_q), .clk(Clock));  // open: clr
  Register #(.width(16)) register_8 (.D(WriteData), .en(decoder_1_out7), .Q(register_8_q), .clk(Clock));  // open: clr
  Multiplexer #(.select(3), .width(16), .enable("false")) multiplexer_1 (
    .in0(register_1_q), .in1(register_2_q), .in2(register_3_q), .in3(register_4_q), .in4(register_5_q),
    .in5(register_6_q), .in6(register_7_q), .in7(register_8_q), .out(ReadData1), .sel(ReadRegister1));
  Multiplexer #(.select(3), .width(16), .enable("false")) multiplexer_2 (
    .in0(register_1_q), .in1(register_2_q), .in2(register_3_q), .in3(register_4_q), .in4(register_5_q),
    .in5(register_6_q), .in6(register_7_q), .in7(register_8_q), .out(ReadData2), .sel(ReadRegister2));
endmodule

module ShifterDecoder (
  input  [3:0] Opcode,
  output ShiftSrc,
  output ShiftertoReg,
  output RegWrite
);

  and and_1 (RegWrite, ~Opcode[3], Opcode[2], ~Opcode[1]);  // AND_Gate

  assign ShiftertoReg = RegWrite;
  assign ShiftSrc = Opcode[0];
endmodule

module Arith_Log_Decoder (
  input  [3:0] Opcode,
  input  Subop,
  output [3:0] ALUOperation,
  output RegWrite,
  output ALUSrc
);

  wire and_1_out, and_3_out, and_4_out, and_5_out, and_6_out, and_7_out, and_8_out, not_1_out, not_2_out,
       not_3_out, not_4_out, not_5_out, not_6_out, not_7_out, not_8_out, not_9_out, not_10_out, not_11_out,
       not_12_out, not_13_out, not_14_out, not_15_out, not_16_out, not_17_out, not_18_out, not_19_out,
       not_20_out, not_21_out;

  and and_1 (and_1_out, ~Opcode[3], ~Opcode[2], Opcode[1], ~Opcode[0], ~Subop);  // AND_Gate
  not not_1 (not_1_out, Opcode[3]);
  not not_2 (not_2_out, Opcode[2]);
  not not_3 (not_3_out, Subop);
  not not_4 (not_4_out, Opcode[3]);
  not not_5 (not_5_out, Opcode[2]);
  not not_6 (not_6_out, Opcode[1]);
  not not_7 (not_7_out, Opcode[0]);
  not not_8 (not_8_out, Opcode[3]);
  not not_9 (not_9_out, Opcode[2]);
  not not_10 (not_10_out, Subop);
  not not_11 (not_11_out, Opcode[3]);
  not not_12 (not_12_out, Opcode[2]);
  not not_13 (not_13_out, Opcode[1]);
  not not_14 (not_14_out, Opcode[3]);
  not not_15 (not_15_out, Opcode[2]);
  not not_16 (not_16_out, Opcode[1]);
  not not_17 (not_17_out, Opcode[3]);
  not not_18 (not_18_out, Opcode[2]);
  not not_19 (not_19_out, Opcode[3]);
  not not_20 (not_20_out, Opcode[2]);
  not not_21 (not_21_out, Opcode[1]);
  and and_2 (ALUOperation[3], not_1_out, not_2_out, Opcode[1], Opcode[0], not_3_out);
  and and_3 (and_3_out, not_4_out, not_5_out, not_6_out, not_7_out, Subop);
  and and_4 (and_4_out, not_8_out, not_9_out, Opcode[1], Opcode[0], not_10_out);
  and and_5 (and_5_out, not_11_out, not_12_out, not_13_out);
  and and_6 (and_6_out, not_14_out, not_15_out, not_16_out);
  and and_7 (and_7_out, ~Opcode[2], Opcode[1]);  // AND_Gate
  and and_8 (and_8_out, not_17_out, not_18_out, Opcode[0]);
  and and_9 (ALUSrc, not_19_out, not_20_out, not_21_out, Opcode[0]);
  or or_1 (ALUOperation[2], and_3_out, and_1_out, and_4_out);
  or or_2 (ALUOperation[1], and_1_out, and_5_out);
  or or_3 (RegWrite, and_6_out, and_7_out, and_8_out);

  assign ALUOperation[0] = 1'b0;
endmodule

module Arith_Log (
  input  Opcode3,
  input  Opcode2,
  input  Opcode1,
  input  Opcode0,
  input  Unsigned,
  input  Subop,
  output ALUOp3,
  output ALUOp2,
  output ALUOp1,
  output ALUOp0,
  output RegWrite,
  output ALUSrc
);

  wire and_2_out, and_3_out, and_5_out, and_6_out, not_1_out, not_2_out, not_3_out, not_4_out, not_5_out,
       not_6_out, not_7_out, not_8_out, not_9_out, not_10_out, not_11_out, not_12_out, not_13_out,
       not_14_out, not_15_out, not_16_out, not_17_out, not_18_out, not_19_out, not_20_out, not_21_out;

  not not_1 (not_1_out, Opcode3);
  not not_2 (not_2_out, Opcode2);
  not not_3 (not_3_out, Subop);
  not not_4 (not_4_out, Opcode3);
  not not_5 (not_5_out, Opcode2);
  not not_6 (not_6_out, Opcode1);
  not not_7 (not_7_out, Opcode0);
  not not_8 (not_8_out, Opcode3);
  not not_9 (not_9_out, Opcode2);
  not not_10 (not_10_out, Subop);
  not not_11 (not_11_out, Opcode3);
  not not_12 (not_12_out, Opcode2);
  not not_13 (not_13_out, Opcode1);
  not not_14 (not_14_out, Opcode3);
  not not_15 (not_15_out, Opcode2);
  not not_16 (not_16_out, Opcode1);
  not not_17 (not_17_out, Opcode3);
  not not_18 (not_18_out, Opcode2);
  not not_19 (not_19_out, Opcode3);
  not not_20 (not_20_out, Opcode2);
  not not_21 (not_21_out, Opcode1);
  and and_1 (ALUOp3, not_1_out, not_2_out, Opcode1, Opcode0, not_3_out);
  and and_2 (and_2_out, not_4_out, not_5_out, not_6_out, not_7_out, Subop);
  and and_3 (and_3_out, not_8_out, not_9_out, Opcode1, Opcode0, not_10_out);
  and and_4 (ALUOp1, not_11_out, not_12_out, not_13_out);
  and and_5 (and_5_out, not_14_out, not_15_out, not_16_out);
  and and_6 (and_6_out, not_17_out, not_18_out, Opcode0);
  and and_7 (ALUSrc, not_19_out, not_20_out, not_21_out, Opcode0);
  or or_1 (ALUOp2, and_2_out, and_3_out);
  or or_2 (RegWrite, and_5_out, and_6_out);

  assign ALUOp0 = 1'b0;
endmodule

module one_bit_ALU (
  input  Ainvert,
  input  Binvert,
  input  CarryIn,
  input  [1:0] Operation,
  input  a,
  input  b,
  input  Less,
  output Result,
  output Set,
  output CarryOut
);

  wire and_1_out, multiplexer_1_out, multiplexer_2_out, not_1_out, not_2_out, or_1_out;

  not not_1 (not_1_out, a);
  Multiplexer #(.enable("false")) multiplexer_1 (.in0(a), .in1(not_1_out), .out(multiplexer_1_out), .sel(Ainvert));
  not not_2 (not_2_out, b);
  Multiplexer #(.enable("false")) multiplexer_2 (.in0(b), .in1(not_2_out), .out(multiplexer_2_out), .sel(Binvert));
  and and_1 (and_1_out, multiplexer_1_out, multiplexer_2_out);
  or or_1 (or_1_out, multiplexer_1_out, multiplexer_2_out);
  Adder #(.width(1)) adder_1 (.a(multiplexer_1_out), .b(multiplexer_2_out), .out(Set), .cin(CarryIn), .cout(CarryOut));
  Multiplexer #(.select(2), .enable("false")) multiplexer_3 (
    .in0(and_1_out), .in1(or_1_out), .in2(Set), .in3(Less), .out(Result), .sel(Operation));
endmodule

module sixteen_bit_ALU (
  input  [3:0] ALUOperation,
  input  [15:0] a,
  input  [15:0] b,
  output Zero,
  output [15:0] Result,
  output Overflow
);

  wire one_bit_alu_1_carryout, one_bit_alu_2_carryout, one_bit_alu_3_carryout, one_bit_alu_4_carryout,
       one_bit_alu_5_carryout, one_bit_alu_6_carryout, one_bit_alu_7_carryout, one_bit_alu_8_carryout,
       one_bit_alu_9_carryout, one_bit_alu_10_carryout, one_bit_alu_11_carryout, one_bit_alu_12_carryout,
       one_bit_alu_13_carryout, one_bit_alu_14_carryout, one_bit_alu_15_carryout, one_bit_alu_16_carryout,
       one_bit_alu_16_set, xor_1_out;

  one_bit_ALU one_bit_alu_1 (
    .a(a[0]), .b(b[0]), .Less(xor_1_out), .Ainvert(ALUOperation[3]), .Binvert(ALUOperation[2]),
    .CarryIn(ALUOperation[2]), .Operation(ALUOperation[1:0]), .CarryOut(one_bit_alu_1_carryout),
    .Result(Result[0]));  // open: Set
  one_bit_ALU one_bit_alu_2 (
    .a(a[1]), .b(b[1]), .Less(1'b0), .Ainvert(ALUOperation[3]), .Binvert(ALUOperation[2]),
    .CarryIn(one_bit_alu_1_carryout), .Operation(ALUOperation[1:0]), .CarryOut(one_bit_alu_2_carryout),
    .Result(Result[1]));  // open: Set
  one_bit_ALU one_bit_alu_3 (
    .a(a[2]), .b(b[2]), .Less(1'b0), .Ainvert(ALUOperation[3]), .Binvert(ALUOperation[2]),
    .CarryIn(one_bit_alu_2_carryout), .Operation(ALUOperation[1:0]), .CarryOut(one_bit_alu_3_carryout),
    .Result(Result[2]));  // open: Set
  one_bit_ALU one_bit_alu_4 (
    .a(a[3]), .b(b[3]), .Less(1'b0), .Ainvert(ALUOperation[3]), .Binvert(ALUOperation[2]),
    .CarryIn(one_bit_alu_3_carryout), .Operation(ALUOperation[1:0]), .CarryOut(one_bit_alu_4_carryout),
    .Result(Result[3]));  // open: Set
  one_bit_ALU one_bit_alu_5 (
    .a(a[4]), .b(b[4]), .Less(1'b0), .Ainvert(ALUOperation[3]), .Binvert(ALUOperation[2]),
    .CarryIn(one_bit_alu_4_carryout), .Operation(ALUOperation[1:0]), .CarryOut(one_bit_alu_5_carryout),
    .Result(Result[4]));  // open: Set
  one_bit_ALU one_bit_alu_6 (
    .a(a[5]), .b(b[5]), .Less(1'b0), .Ainvert(ALUOperation[3]), .Binvert(ALUOperation[2]),
    .CarryIn(one_bit_alu_5_carryout), .Operation(ALUOperation[1:0]), .CarryOut(one_bit_alu_6_carryout),
    .Result(Result[5]));  // open: Set
  one_bit_ALU one_bit_alu_7 (
    .a(a[6]), .b(b[6]), .Less(1'b0), .Ainvert(ALUOperation[3]), .Binvert(ALUOperation[2]),
    .CarryIn(one_bit_alu_6_carryout), .Operation(ALUOperation[1:0]), .CarryOut(one_bit_alu_7_carryout),
    .Result(Result[6]));  // open: Set
  one_bit_ALU one_bit_alu_8 (
    .a(a[7]), .b(b[7]), .Less(1'b0), .Ainvert(ALUOperation[3]), .Binvert(ALUOperation[2]),
    .CarryIn(one_bit_alu_7_carryout), .Operation(ALUOperation[1:0]), .CarryOut(one_bit_alu_8_carryout),
    .Result(Result[7]));  // open: Set
  one_bit_ALU one_bit_alu_9 (
    .a(a[8]), .b(b[8]), .Less(1'b0), .Ainvert(ALUOperation[3]), .Binvert(ALUOperation[2]),
    .CarryIn(one_bit_alu_8_carryout), .Operation(ALUOperation[1:0]), .CarryOut(one_bit_alu_9_carryout),
    .Result(Result[8]));  // open: Set
  one_bit_ALU one_bit_alu_10 (
    .a(a[9]), .b(b[9]), .Less(1'b0), .Ainvert(ALUOperation[3]), .Binvert(ALUOperation[2]),
    .CarryIn(one_bit_alu_9_carryout), .Operation(ALUOperation[1:0]), .CarryOut(one_bit_alu_10_carryout),
    .Result(Result[9]));  // open: Set
  one_bit_ALU one_bit_alu_11 (
    .a(a[10]), .b(b[10]), .Less(1'b0), .Ainvert(ALUOperation[3]), .Binvert(ALUOperation[2]),
    .CarryIn(one_bit_alu_10_carryout), .Operation(ALUOperation[1:0]), .CarryOut(one_bit_alu_11_carryout),
    .Result(Result[10]));  // open: Set
  one_bit_ALU one_bit_alu_12 (
    .a(a[11]), .b(b[11]), .Less(1'b0), .Ainvert(ALUOperation[3]), .Binvert(ALUOperation[2]),
    .CarryIn(one_bit_alu_11_carryout), .Operation(ALUOperation[1:0]), .CarryOut(one_bit_alu_12_carryout),
    .Result(Result[11]));  // open: Set
  one_bit_ALU one_bit_alu_13 (
    .a(a[12]), .b(b[12]), .Less(1'b0), .Ainvert(ALUOperation[3]), .Binvert(ALUOperation[2]),
    .CarryIn(one_bit_alu_12_carryout), .Operation(ALUOperation[1:0]), .CarryOut(one_bit_alu_13_carryout),
    .Result(Result[12]));  // open: Set
  one_bit_ALU one_bit_alu_14 (
    .a(a[13]), .b(b[13]), .Less(1'b0), .Ainvert(ALUOperation[3]), .Binvert(ALUOperation[2]),
    .CarryIn(one_bit_alu_13_carryout), .Operation(ALUOperation[1:0]), .CarryOut(one_bit_alu_14_carryout),
    .Result(Result[13]));  // open: Set
  one_bit_ALU one_bit_alu_15 (
    .a(a[14]), .b(b[14]), .Less(1'b0), .Ainvert(ALUOperation[3]), .Binvert(ALUOperation[2]),
    .CarryIn(one_bit_alu_14_carryout), .Operation(ALUOperation[1:0]), .CarryOut(one_bit_alu_15_carryout),
    .Result(Result[14]));  // open: Set
  one_bit_ALU one_bit_alu_16 (
    .a(a[15]), .b(b[15]), .Less(1'b0), .Ainvert(ALUOperation[3]), .Binvert(ALUOperation[2]),
    .CarryIn(one_bit_alu_15_carryout), .Operation(ALUOperation[1:0]), .CarryOut(one_bit_alu_16_carryout),
    .Result(Result[15]), .Set(one_bit_alu_16_set));
  xor xor_1 (xor_1_out, one_bit_alu_16_set, Overflow);
  xor xor_2 (Overflow, one_bit_alu_15_carryout, one_bit_alu_16_carryout);
  nor nor_1 (Zero, Result[0], Result[1], Result[2], Result[3], Result[4], Result[5], Result[6], Result[7], Result[8], Result[9], Result[10], Result[11], Result[12], Result[13], Result[14], Result[15]);
endmodule

module PCDecoder (
  input  [3:0] Opcode,
  input  Subop,
  input  Zero,
  input  Less,
  output RegtoPC,
  output IMMtoPC,
  output ZerosToALU,
  output [3:0] ALUOp
);

  wire and_4_out, and_5_out, and_6_out, and_7_out, and_8_out, not_1_out, not_2_out, not_3_out, not_4_out,
       not_5_out, not_6_out, not_7_out, not_8_out, not_9_out, not_10_out, not_11_out, not_12_out, not_13_out,
       not_14_out, not_15_out, not_16_out;

  not not_1 (not_1_out, Opcode[2]);
  not not_2 (not_2_out, Opcode[1]);
  not not_3 (not_3_out, Subop);
  not not_4 (not_4_out, Opcode[2]);
  not not_5 (not_5_out, Opcode[1]);
  not not_6 (not_6_out, Opcode[0]);
  not not_7 (not_7_out, Opcode[2]);
  not not_8 (not_8_out, Opcode[1]);
  not not_9 (not_9_out, Zero);
  not not_10 (not_10_out, Opcode[2]);
  not not_11 (not_11_out, Zero);
  not not_12 (not_12_out, Opcode[0]);
  not not_13 (not_13_out, Zero);
  not not_14 (not_14_out, Less);
  not not_15 (not_15_out, Opcode[0]);
  and and_1 (ZerosToALU, Opcode[3], not_16_out);
  not not_16 (not_16_out, Opcode[2]);
  and and_2 (ALUOp[1], Opcode[3], not_1_out);
  and and_3 (RegtoPC, Opcode[3], Opcode[2], not_2_out, Opcode[0], not_3_out);
  and and_4 (and_4_out, Opcode[3], not_4_out, not_5_out, not_6_out, Zero);
  and and_5 (and_5_out, Opcode[3], not_7_out, not_8_out, Opcode[0], not_9_out);
  and and_6 (and_6_out, Opcode[3], not_10_out, Opcode[0], not_11_out, Less);
  and and_7 (and_7_out, Opcode[3], Opcode[1], not_12_out, not_13_out, not_14_out);
  and and_8 (and_8_out, Opcode[3], Opcode[2], Opcode[1], not_15_out);
  or or_1 (IMMtoPC, and_4_out, and_5_out, and_6_out, and_7_out, and_8_out);

  assign {ALUOp[3:2], ALUOp[0]} = 3'b000;
endmodule

module PCDecoderLogic (
  input  Opcode3,
  input  Opcode2,
  input  Opcode1,
  input  Opcode0,
  input  Subop,
  input  Zero,
  input  Less,
  output RegtoPC,
  output IMMtoPC,
  output OnestoALU
);

  wire and_2_out, and_3_out, and_4_out, and_5_out, and_6_out, not_1_out, not_2_out, not_3_out, not_4_out,
       not_5_out, not_6_out, not_7_out, not_8_out, not_9_out, not_10_out, not_11_out, not_12_out, not_13_out,
       not_14_out, not_15_out;

  not not_1 (not_1_out, Opcode1);
  not not_2 (not_2_out, Subop);
  not not_3 (not_3_out, Opcode2);
  not not_4 (not_4_out, Opcode1);
  not not_5 (not_5_out, Opcode0);
  not not_6 (not_6_out, Opcode2);
  not not_7 (not_7_out, Opcode1);
  not not_8 (not_8_out, Zero);
  not not_9 (not_9_out, Opcode2);
  not not_10 (not_10_out, Zero);
  not not_11 (not_11_out, Opcode0);
  not not_12 (not_12_out, Zero);
  not not_13 (not_13_out, Less);
  not not_14 (not_14_out, Opcode0);
  not not_15 (not_15_out, Opcode2);
  and and_1 (RegtoPC, Opcode3, Opcode2, not_1_out, Opcode0, not_2_out);
  and and_2 (and_2_out, Opcode3, not_3_out, not_4_out, not_5_out, Zero);
  and and_3 (and_3_out, Opcode3, not_6_out, not_7_out, Opcode0, not_8_out);
  and and_4 (and_4_out, Opcode3, not_9_out, Opcode0, not_10_out, Less);
  and and_5 (and_5_out, Opcode3, Opcode1, not_11_out, not_12_out, not_13_out);
  and and_6 (and_6_out, Opcode3, Opcode2, Opcode1, not_14_out);
  and and_7 (OnestoALU, Opcode3, not_15_out);
  or or_1 (IMMtoPC, and_2_out, and_3_out, and_4_out, and_5_out, and_6_out);
endmodule

module Decoder (
  input  [3:0] Opcode,
  input  Subop,
  input  Zero,
  input  Less,
  output ShiftSrc,
  output ShifterToReg,
  output RegWrite,
  output [3:0] ALUOp,
  output IMMtoALU,
  output RegtoPC,
  output IMMtoPC,
  output ZerosToALU,
  output MemWrite,
  output MemtoReg,
  output Halt,
  output LED,
  output WriteLED,
  output MemRead,
  output PCtoReg
);

  wire Arith_LogDecoder_regwrite, JALDecoder_immtopc, JALDecoder_regwrite, MemDecoder_regwrite,
       PCDecoder_immtopc, ShifterDecoder_regwrite;
  wire [3:0] Arith_LogDecoder_aluoperation, PCDecoder_aluop;

  ShifterDecoder ShifterDecoder (
    .Opcode(Opcode), .ShiftSrc(ShiftSrc), .ShiftertoReg(ShifterToReg), .RegWrite(ShifterDecoder_regwrite));
  Arith_Log_Decoder Arith_LogDecoder (
    .Opcode(Opcode), .Subop(Subop), .ALUOperation(Arith_LogDecoder_aluoperation),
    .RegWrite(Arith_LogDecoder_regwrite), .ALUSrc(IMMtoALU));
  PCDecoder PCDecoder (
    .Opcode(Opcode), .Subop(Subop), .Zero(Zero), .Less(Less), .RegtoPC(RegtoPC), .IMMtoPC(PCDecoder_immtopc),
    .ZerosToALU(ZerosToALU), .ALUOp(PCDecoder_aluop));
  MemDecoder MemDecoder (
    .Opcode(Opcode), .Subop(Subop), .MemWrite(MemWrite), .MemtoReg(MemtoReg), .RegWrite(MemDecoder_regwrite),
    .MemRead(MemRead));
  HaltDecoder haltdecoder_1 (.Opcode(Opcode), .Halt(Halt), .LED(LED));
  PutDecoder PutDecoder (.Opcode(Opcode), .WriteLED(WriteLED));
  JALDecoder JALDecoder (
    .Opcode(Opcode), .IMMtoPC(JALDecoder_immtopc), .PCtoReg(PCtoReg), .RegWrite(JALDecoder_regwrite));
  or or_1 (RegWrite, ShifterDecoder_regwrite, Arith_LogDecoder_regwrite, MemDecoder_regwrite, JALDecoder_regwrite);
  or or_2 (IMMtoPC, PCDecoder_immtopc, JALDecoder_immtopc);
  assign ALUOp = Arith_LogDecoder_aluoperation | PCDecoder_aluop;  // OR_Gate or_3, 4 bits wide
endmodule

module MemDecoder (
  input  [3:0] Opcode,
  input  Subop,
  output MemWrite,
  output MemtoReg,
  output RegWrite,
  output MemRead
);

  and and_1 (MemWrite, ~Opcode[0], Opcode[1], Opcode[2], ~Opcode[3], Subop);  // AND_Gate
  and and_2 (MemRead, ~Opcode[0], Opcode[1], Opcode[2], ~Opcode[3], ~Subop);  // AND_Gate

  assign MemtoReg = MemRead;
  assign RegWrite = MemRead;
endmodule

module HaltDecoder (
  input  [3:0] Opcode,
  output Halt,
  output LED
);

  and and_1 (Halt, ~Opcode[3], Opcode[2], Opcode[1], Opcode[0]);  // AND_Gate

  assign LED = Halt;
endmodule

module PutDecoder (
  input  [3:0] Opcode,
  output WriteLED
);

  and and_1 (WriteLED, Opcode[0], Opcode[1], Opcode[2], Opcode[3]);
endmodule

module JALDecoder (
  input  [3:0] Opcode,
  output IMMtoPC,
  output PCtoReg,
  output RegWrite
);

  and and_1 (IMMtoPC, ~Opcode[0], ~Opcode[1], Opcode[2], Opcode[3]);  // AND_Gate

  assign PCtoReg = IMMtoPC;
  assign RegWrite = IMMtoPC;
endmodule

module ResultToLess (
  input  [15:0] Result,
  output Less
);


  assign Less = Result[15];
endmodule

module side (
  input  Op3,
  input  Op2,
  input  Op1,
  input  Op0,
  output Op3_2,
  output Op2_2,
  output Op1_2,
  output Op0_2
);

  wire not_1_out;

  and and_1 (Op1_2, Op3, not_1_out);
  not not_1 (not_1_out, Op2);

  assign Op0_2 = 1'b0;
  assign Op2_2 = 1'b0;
  assign Op3_2 = 1'b0;
endmodule

module forwardingUnit (
  input  EX_MEM_RegWrite,
  input  [2:0] ID_EX_Rs,
  input  [2:0] EX_MEM_Rs,
  input  [2:0] ID_EX_Rt,
  input  [2:0] MEM_WB_Rs,
  input  MEM_WB_RegWrite,
  output [1:0] AluMuxA,
  output [1:0] AluMuxB,
  output C
);

  wire and_5_out, comparator_1_eq, comparator_2_eq, comparator_3_eq, comparator_4_eq, comparator_5_eq;
  wire [1:0] and_3_out, and_4_out;

  Comparator #(.width(3)) comparator_1 (.a(ID_EX_Rs), .b(EX_MEM_Rs), .eq(comparator_1_eq));  // open: gt, lt
  Comparator #(.width(3)) comparator_2 (.a(EX_MEM_Rs), .b(ID_EX_Rt), .eq(comparator_2_eq));  // open: gt, lt
  Comparator #(.width(3)) comparator_3 (.a(ID_EX_Rs), .b(MEM_WB_Rs), .eq(comparator_3_eq));  // open: gt, lt
  Comparator #(.width(3)) comparator_4 (.a(MEM_WB_Rs), .b(ID_EX_Rt), .eq(comparator_4_eq));  // open: gt, lt
  and and_1 (and_4_out[1], EX_MEM_RegWrite, comparator_1_eq);
  and and_2 (and_3_out[1], EX_MEM_RegWrite, comparator_2_eq);
  and and_3 (and_3_out[0], MEM_WB_RegWrite, comparator_4_eq, ~and_3_out[1]);  // AND_Gate
  and and_4 (and_4_out[0], MEM_WB_RegWrite, comparator_3_eq, ~and_4_out[1]);  // AND_Gate
  Comparator #(.width(3)) comparator_5 (.a(EX_MEM_Rs), .b(MEM_WB_Rs), .eq(comparator_5_eq));  // open: gt, lt
  Multiplexer #(.select(2), .width(2), .enable("false")) multiplexer_1 (
    .in0(2'b00), .in1(2'b01), .in2(2'b10), .out(AluMuxA), .sel(and_4_out));  // open: in3
  Multiplexer #(.select(2), .width(2), .enable("false")) multiplexer_2 (
    .in0(2'b00), .in1(2'b01), .in2(2'b10), .out(AluMuxB), .sel(and_3_out));  // open: in3
  and and_5 (and_5_out, MEM_WB_RegWrite, EX_MEM_RegWrite, comparator_5_eq);
  not not_1 (C, and_5_out);

  // Notes on the sheet:
  //   10
  //   10
  //   01
  //   01
endmodule

module hazardUnit (
  input  ID_EX_MemRead,
  input  [2:0] IF_ID_Rs,
  input  [2:0] ID_EX_Rs,
  input  [2:0] IF_ID_Rt,
  output PCWrite,
  output IF_EX_Write,
  output Bubble
);

  wire comparator_1_eq, comparator_2_eq, or_1_out;

  Comparator #(.width(3)) comparator_1 (.a(IF_ID_Rs), .b(ID_EX_Rs), .eq(comparator_1_eq));  // open: gt, lt
  Comparator #(.width(3)) comparator_2 (.a(ID_EX_Rs), .b(IF_ID_Rt), .eq(comparator_2_eq));  // open: gt, lt
  or or_1 (or_1_out, comparator_1_eq, comparator_2_eq);
  and and_1 (Bubble, ID_EX_MemRead, or_1_out);
  not not_1 (IF_EX_Write, Bubble);

  assign PCWrite = IF_EX_Write;
endmodule

module VARUN (
);

  wire AluZero, and_1_out, Bubble, button_1_out, C, clock_1_out, Decoder_immtoalu, Decoder_immtopc,
       Decoder_led, Decoder_memread, Decoder_memtoreg, Decoder_memwrite, Decoder_pctoreg, Decoder_regtopc,
       Decoder_regwrite, Decoder_shiftertoreg, Decoder_shiftsrc, Decoder_writeled, Decoder_zerostoalu,
       EX_MEM_Buffer_mem_halt, EX_MEM_Buffer_mem_led, EX_MEM_Buffer_mem_memtoreg, EX_MEM_Buffer_mem_writeled,
       EX_MemRead, Halt, ID_EX_Buffer_ex_halt, ID_EX_Buffer_ex_led, ID_EX_Buffer_ex_memtoreg,
       ID_EX_Buffer_ex_memwrite, ID_EX_Buffer_ex_regwrite, ID_EX_Buffer_ex_writeled, IF_EX_Write, IMMtoALU,
       IMMtoPC, Instruction_Splitter_subop, Instruction_Splitter_unsigned, LED, MEM_MemRead, MEM_MemWrite,
       MEM_RegWrite, not_1_out, or_1_out, PCWrite, RegToPC, ResultToLess_less, s_r_ff_1_q, undriven,
       WB_MemToReg, WB_RegWrite, WriteLED, ZerosToALU;
  wire [1:0] AluMuxA, AluMuxB;
  wire [2:0] EX_MEM_Buffer_mem_rt, EX_Rs, EX_Rt, ID_Rs, ID_Rt, MEM_Rs, WB_Rs;
  wire [3:0] AluOp, Decoder_aluop, Instruction_Splitter_opcode, Instruction_Splitter_shiftamount;
  wire [7:0] adder_1_out, IF_PC, Instruction_Splitter_immediate, multiplexer_3_out, multiplexer_5_out, PC_q,
       RegistertoAddress_2_address, RegistertoAddress_address;
  wire [15:0] AluResult, bit_extender_1_out, EX_AluResult, EX_imm, EX_MemWriteData, EX_Rs_data, EX_Rt_data,
       ID_imm, ID_Rs_data, ID_Rt_data, IF_ID_Buffer_id_instructions, LedData, MEM_AluResult, MEM_MemReadData,
       MEM_MemWriteData, multiplexer_2_out, multiplexer_4_out, multiplexer_6_out, multiplexer_7_out,
       multiplexer_8_out, multiplexer_9_out, multiplexer_10_out, register_1_q, register_2_q, register_3_q,
       register_4_q, register_6_q, rom_1_data, Shifter_shiftout, undriven_2, WB_AluResult, WB_MemReadData,
       WB_WriteBackValue;

  LED u_Halt (.in(not_1_out));
  not not_1 (not_1_out, and_1_out);
  Clock clock_1 (.out(clock_1_out));
  Register #(.width(16)) register_1 (.D(rom_1_data), .Q(register_1_q), .clk(clock_1_out));  // open: en, clr
  Register #(.trigger("falling")) PC (
    .D(multiplexer_5_out), .en(and_1_out), .Q(PC_q), .clk(clock_1_out), .clr(button_1_out));
  and and_1 (and_1_out, PCWrite, ~s_r_ff_1_q);  // AND_Gate
  S_R_Flip_Flop s_r_ff_1 (.clk(clock_1_out), .Q(s_r_ff_1_q), .preset(Halt), .en(1'b1));  // open: S, R, Qn, reset
  Register #(.width(16)) register_2 (.D(register_1_q), .Q(register_2_q), .clk(clock_1_out));  // open: en, clr
  Button button_1 (.out(button_1_out));
  Register #(.width(16)) register_3 (.D(register_2_q), .Q(register_3_q), .clk(clock_1_out));  // open: en, clr
  Adder adder_1 (.a(PC_q), .b(8'h1), .out(adder_1_out));  // open: cin, cout
  Register #(.width(16)) register_4 (.D(register_3_q), .Q(register_4_q), .clk(clock_1_out));  // open: en, clr
  hazardUnit hazardUnit (
    .ID_EX_MemRead(EX_MemRead), .IF_ID_Rs(ID_Rs), .ID_EX_Rs(EX_Rs), .IF_ID_Rt(ID_Rt), .PCWrite(PCWrite),
    .IF_EX_Write(IF_EX_Write), .Bubble(Bubble));
  ROM #(.dataWidth(16)) rom_1 (.addr(PC_q), .data(rom_1_data), .sel(1'b1));
  Register #(.width(16)) register_5 (.D(register_4_q), .clk(clock_1_out));  // open: en, Q, clr
  IF_ID_Buffer IF_ID_Buffer (
    .IF_Instructions(rom_1_data), .IF_PC(PC_q), .ID_Instructions(IF_ID_Buffer_id_instructions),
    .IF_PC_2(IF_PC), .CLK(clock_1_out), .Enable(PCWrite), .RST(1'b0));
  LINE line_1 ();
  InstructionSplitter Instruction_Splitter (
    .Instruction(IF_ID_Buffer_id_instructions), .Opcode(Instruction_Splitter_opcode), .ReadRegister1(ID_Rs),
    .ReadRegister2(ID_Rt), .ShiftAmount(Instruction_Splitter_shiftamount),
    .SubOp(Instruction_Splitter_subop), .Unsigned(Instruction_Splitter_unsigned),
    .Immediate(Instruction_Splitter_immediate));  // open: WriteRegister
  SignExtend Sign_Extend (
    .Unsigned(Instruction_Splitter_unsigned), .Immediate(Instruction_Splitter_immediate),
    .SignExtendedImm(ID_imm));
  ResultToLess ResultToLess (.Result(EX_AluResult), .Less(ResultToLess_less));
  or or_1 (or_1_out, Bubble, 1'b0);
  RegisterFile Registers (
    .ReadRegister1(ID_Rs), .ReadRegister2(ID_Rt), .WriteRegister(WB_Rs), .WriteData(WB_WriteBackValue),
    .WriteEnable(WB_RegWrite), .Clock(clock_1_out), .ReadData1(ID_Rs_data), .ReadData2(ID_Rt_data));
  Decoder Decoder (
    .Opcode(Instruction_Splitter_opcode), .Subop(Instruction_Splitter_subop), .Zero(AluZero),
    .Less(ResultToLess_less), .ShiftSrc(Decoder_shiftsrc), .ShifterToReg(Decoder_shiftertoreg),
    .RegWrite(Decoder_regwrite), .ALUOp(Decoder_aluop), .IMMtoALU(Decoder_immtoalu),
    .RegtoPC(Decoder_regtopc), .IMMtoPC(Decoder_immtopc), .ZerosToALU(Decoder_zerostoalu),
    .MemWrite(Decoder_memwrite), .MemtoReg(Decoder_memtoreg), .Halt(Halt), .LED(Decoder_led),
    .WriteLED(Decoder_writeled), .MemRead(Decoder_memread), .PCtoReg(Decoder_pctoreg));
  LINE line_2 ();
  ID_EX_Buffer ID_EX_Buffer (
    .ID_RegWrite(Decoder_regwrite), .ID_MemWrite(Decoder_memwrite), .ID_MemtoReg(Decoder_memtoreg),
    .ID_AluOp(Decoder_aluop), .ID_IMMtoALU(Decoder_immtoalu), .ID_RegtoPC(Decoder_regtopc),
    .ID_IMMtoPC(Decoder_immtopc), .ID_ZerosToALU(Decoder_zerostoalu), .ID_Halt(Halt), .ID_LED(Decoder_led),
    .ID_WriteLED(Decoder_writeled), .ID_MemRead(Decoder_memread), .ID_Rs_data(ID_Rs_data),
    .ID_Rt_data(ID_Rt_data), .ID_Rs(ID_Rs), .ID_Rt(ID_Rt), .EX_RegWrite(ID_EX_Buffer_ex_regwrite),
    .EX_MemWrite(ID_EX_Buffer_ex_memwrite), .EX_MemtoReg(ID_EX_Buffer_ex_memtoreg), .EX_AluOp(AluOp),
    .EX_IMMtoALU(IMMtoALU), .EX_RegtoPC(RegToPC), .EX_IMMtoPC(IMMtoPC), .EX_ZerosToALU(ZerosToALU),
    .EX_Halt(ID_EX_Buffer_ex_halt), .EX_LED(ID_EX_Buffer_ex_led), .EX_WriteLED(ID_EX_Buffer_ex_writeled),
    .EX_MemRead(EX_MemRead), .EX_Rs_data(EX_Rs_data), .EX_Rt_data(EX_Rt_data), .EX_Rs(EX_Rs), .EX_Rt(EX_Rt),
    .CLK(clock_1_out), .Enable(1'b1), .RST(or_1_out), .ID_immediate(ID_imm), .EX_immediate(EX_imm));
  ALUtoPC RegistertoAddress (.ALUOut(EX_Rs_data), .Address(RegistertoAddress_address));
  Multiplexer #(.select(2), .width(16), .disabled(0), .enable("false")) multiplexer_1 (
    .in0(EX_Rs_data), .in1(WB_WriteBackValue), .in2(MEM_AluResult), .out(EX_MemWriteData), .sel(AluMuxA));  // open: in3
  Multiplexer #(.select(2), .width(16), .disabled(0), .enable("false")) multiplexer_2 (
    .in0(EX_Rt_data), .in1(WB_WriteBackValue), .in2(MEM_AluResult), .out(multiplexer_2_out), .sel(AluMuxB));  // open: in3
  Multiplexer #(.width(8), .disabled(0), .enable("false")) multiplexer_3 (
    .in0(adder_1_out), .in1(Instruction_Splitter_immediate), .out(multiplexer_3_out), .sel(IMMtoPC));
  Multiplexer #(.width(16), .disabled(0), .enable("false")) multiplexer_4 (
    .in0(multiplexer_2_out), .in1(EX_imm), .out(multiplexer_4_out), .sel(IMMtoALU));
  Multiplexer #(.width(8), .disabled(0), .enable("false")) multiplexer_5 (
    .in0(multiplexer_3_out), .in1(RegistertoAddress_address), .out(multiplexer_5_out), .sel(RegToPC));
  Multiplexer #(.width(16), .disabled(0), .enable("false")) multiplexer_6 (
    .in0(multiplexer_4_out), .in1({16{1'b0}}), .out(multiplexer_6_out), .sel(ZerosToALU));
  Shifter Shifter (
    .Subop(Instruction_Splitter_subop), .Data(EX_Rs_data), .ShamtReg(EX_Rt_data),
    .ShiftSrc(Decoder_shiftsrc), .Shamt(Instruction_Splitter_shiftamount), .ShiftOut(Shifter_shiftout));
  assign bit_extender_1_out = {{8{1'b0}}, adder_1_out};  // Bit_Extender bit_extender_1
  EX_MEM_Buffer EX_MEM_Buffer (
    .EX_RegWrite(ID_EX_Buffer_ex_regwrite), .EX_MemWrite(ID_EX_Buffer_ex_memwrite),
    .EX_MemtoReg(ID_EX_Buffer_ex_memtoreg), .EX_Halt(ID_EX_Buffer_ex_halt), .EX_LED(ID_EX_Buffer_ex_led),
    .EX_WriteLED(ID_EX_Buffer_ex_writeled), .EX_MemRead(EX_MemRead), .EX_AluResult(EX_AluResult),
    .EX_Rs(EX_Rs), .EX_Rt(EX_Rt), .MEM_RegWrite(MEM_RegWrite), .MEM_MemWrite(MEM_MemWrite),
    .MEM_MemtoReg(EX_MEM_Buffer_mem_memtoreg), .MEM_Halt(EX_MEM_Buffer_mem_halt),
    .MEM_LED(EX_MEM_Buffer_mem_led), .MEM_WriteLED(EX_MEM_Buffer_mem_writeled), .MEM_MemRead(MEM_MemRead),
    .MEM_AluResult(MEM_AluResult), .MEM_Rs(MEM_Rs), .MEM_Rt(EX_MEM_Buffer_mem_rt), .CLK(clock_1_out),
    .Enable(1'b1), .RST(1'b0), .EX_MemWriteData(EX_MemWriteData), .MEM_MemWriteData(MEM_MemWriteData));
  sixteen_bit_ALU ALU (
    .ALUOperation(AluOp), .a(EX_MemWriteData), .b(multiplexer_6_out), .Zero(AluZero), .Result(EX_AluResult));  // open: Overflow
  LINE line_3 ();
  MEM_WB_Buffer MEM_WB_Buffer (
    .MEM_RegWrite(MEM_RegWrite), .MEM_MemReadData(MEM_MemReadData), .EX_MemtoReg(EX_MEM_Buffer_mem_memtoreg),
    .MEM_AluResult(MEM_AluResult), .MEM_Rs(MEM_Rs), .MEM_Rt(EX_MEM_Buffer_mem_rt), .WB_RegWrite(WB_RegWrite),
    .WB_MemReadData(WB_MemReadData), .WB_MemtoReg(WB_MemToReg), .WB_AluResult(WB_AluResult), .WB_Rs(WB_Rs),
    .CLK(clock_1_out), .Enable(1'b1), .RST(1'b0), .MEM_Halt(EX_MEM_Buffer_mem_halt),
    .MEM_LED(EX_MEM_Buffer_mem_led), .WB_LED(LED), .MEM_WriteLED(EX_MEM_Buffer_mem_writeled),
    .WB_WriteLED(WriteLED), .MEM_MemWriteData(MEM_MemWriteData), .WB_MemWriteData(LedData));  // open: WB_Rt, WB_Halt
  Multiplexer #(.width(16), .disabled(0), .enable("false")) multiplexer_7 (
    .in0(WB_MemReadData), .in1(MEM_MemWriteData), .out(multiplexer_7_out), .sel(C));
  ALUtoPC RegistertoAddress_2 (.ALUOut(MEM_AluResult), .Address(RegistertoAddress_2_address));
  Multiplexer #(.width(16), .disabled(0), .enable("false")) multiplexer_8 (
    .in0(multiplexer_9_out), .in1(bit_extender_1_out), .out(multiplexer_8_out), .sel(Decoder_pctoreg));
  Multiplexer #(.width(16), .disabled(0), .enable("false")) multiplexer_9 (
    .in0(multiplexer_10_out), .in1(Shifter_shiftout), .out(multiplexer_9_out), .sel(Decoder_shiftertoreg));
  RAM #(.dataWidth(16), .bus("separate")) ram_1 (
    .addr(RegistertoAddress_2_address), .din(multiplexer_7_out), .data(MEM_MemReadData), .str(MEM_MemWrite),
    .sel(1'b1), .clk(clock_1_out), .ld(MEM_MemRead), .clr(1'b0));
  forwardingUnit forwardingUnit (
    .EX_MEM_RegWrite(MEM_RegWrite), .ID_EX_Rs(EX_Rs), .EX_MEM_Rs(MEM_Rs), .ID_EX_Rt(EX_Rt),
    .MEM_WB_Rs(WB_Rs), .MEM_WB_RegWrite(WB_RegWrite), .AluMuxA(AluMuxA), .AluMuxB(AluMuxB), .C(C));
  LINE line_4 ();
  Multiplexer #(.width(16), .disabled(0), .enable("false")) multiplexer_10 (
    .in0(AluResult), .in1(undriven_2), .out(multiplexer_10_out), .sel(undriven));
  Register #(.width(16)) register_6 (.D(LedData), .en(WriteLED), .Q(register_6_q), .clk(clock_1_out), .clr(1'b0));
  Multiplexer #(.width(16), .disabled(0), .enable("false")) multiplexer_11 (
    .in0(WB_AluResult), .in1(WB_MemReadData), .out(WB_WriteBackValue), .sel(WB_MemToReg));
  Hex_Digit_Display hex_digit_display_1 (.value(register_6_q[11:8]));  // open: dp
  Hex_Digit_Display hex_digit_display_2 (.value(register_6_q[15:12]));  // open: dp
  Hex_Digit_Display hex_digit_display_3 (.value(register_6_q[3:0]));  // open: dp
  Hex_Digit_Display hex_digit_display_4 (.value(register_6_q[7:4]));  // open: dp

  // Notes on the sheet:
  //   IF
  //   contents of rom_1 (hex, n*v repeats v):
  //   16f6 1914 1206 1afe 1d03 8c0 22c0 b80 f600 f200 f800 fa00 7000
  //   ID
  //   EX
  //   MEM
  //   WB
endmodule

module EX_MEM_Buffer (
  input  CLK,
  input  Enable,
  input  RST,
  input  EX_RegWrite,
  input  EX_MemWrite,
  input  EX_MemtoReg,
  input  EX_Halt,
  input  EX_LED,
  input  EX_WriteLED,
  input  EX_MemRead,
  input  [15:0] EX_AluResult,
  input  [2:0] EX_Rs,
  input  [2:0] EX_Rt,
  input  [15:0] EX_MemWriteData,
  output MEM_RegWrite,
  output MEM_MemWrite,
  output MEM_MemtoReg,
  output MEM_Halt,
  output MEM_LED,
  output MEM_WriteLED,
  output MEM_MemRead,
  output [15:0] MEM_AluResult,
  output [2:0] MEM_Rs,
  output [2:0] MEM_Rt,
  output [15:0] MEM_MemWriteData
);

  Register #(.width(1), .trigger("falling")) register_1 (
    .D(EX_RegWrite), .en(Enable), .Q(MEM_RegWrite), .clk(CLK), .clr(RST));
  Register #(.width(1), .trigger("falling")) register_2 (
    .D(EX_MemWrite), .en(Enable), .Q(MEM_MemWrite), .clk(CLK), .clr(RST));
  Register #(.width(1), .trigger("falling")) register_3 (
    .D(EX_MemtoReg), .en(Enable), .Q(MEM_MemtoReg), .clk(CLK), .clr(RST));
  Register #(.width(1), .trigger("falling")) register_4 (.D(EX_Halt), .en(Enable), .Q(MEM_Halt), .clk(CLK), .clr(RST));
  Register #(.width(1), .trigger("falling")) register_5 (.D(EX_LED), .en(Enable), .Q(MEM_LED), .clk(CLK), .clr(RST));
  Register #(.width(1), .trigger("falling")) register_6 (
    .D(EX_WriteLED), .en(Enable), .Q(MEM_WriteLED), .clk(CLK), .clr(RST));
  Register #(.width(1), .trigger("falling")) register_7 (
    .D(EX_MemRead), .en(Enable), .Q(MEM_MemRead), .clk(CLK), .clr(RST));
  Register #(.width(16), .trigger("falling")) register_8 (
    .D(EX_AluResult), .en(Enable), .Q(MEM_AluResult), .clk(CLK), .clr(RST));
  Register #(.width(3), .trigger("falling")) register_9 (.D(EX_Rs), .en(Enable), .Q(MEM_Rs), .clk(CLK), .clr(RST));
  Register #(.width(3), .trigger("falling")) register_10 (.D(EX_Rt), .en(Enable), .Q(MEM_Rt), .clk(CLK), .clr(RST));
  Register #(.width(16), .trigger("falling")) register_11 (
    .D(EX_MemWriteData), .en(Enable), .Q(MEM_MemWriteData), .clk(CLK), .clr(RST));

  // Notes on the sheet:
  //   EX/MEM
endmodule

module IF_ID_Buffer (
  input  CLK,
  input  Enable,
  input  RST,
  input  [15:0] IF_Instructions,
  input  [7:0] IF_PC,
  output [15:0] ID_Instructions,
  output [7:0] IF_PC_2
);

  Register #(.width(16), .trigger("falling")) register_1 (
    .D(IF_Instructions), .en(Enable), .Q(ID_Instructions), .clk(CLK), .clr(RST));
  Register #(.trigger("falling")) register_2 (.D(IF_PC), .en(Enable), .Q(IF_PC_2), .clk(CLK), .clr(RST));
endmodule

module ID_EX_Buffer (
  input  CLK,
  input  Enable,
  input  RST,
  input  ID_RegWrite,
  input  ID_MemWrite,
  input  ID_MemtoReg,
  input  [3:0] ID_AluOp,
  input  ID_IMMtoALU,
  input  ID_RegtoPC,
  input  ID_IMMtoPC,
  input  ID_ZerosToALU,
  input  ID_Halt,
  input  ID_LED,
  input  ID_WriteLED,
  input  ID_MemRead,
  input  [15:0] ID_Rs_data,
  input  [15:0] ID_Rt_data,
  input  [2:0] ID_Rs,
  input  [2:0] ID_Rt,
  input  [15:0] ID_immediate,
  output EX_RegWrite,
  output EX_MemWrite,
  output EX_MemtoReg,
  output [3:0] EX_AluOp,
  output EX_IMMtoALU,
  output EX_RegtoPC,
  output EX_IMMtoPC,
  output EX_ZerosToALU,
  output EX_Halt,
  output EX_LED,
  output EX_WriteLED,
  output EX_MemRead,
  output [15:0] EX_Rs_data,
  output [15:0] EX_Rt_data,
  output [2:0] EX_Rs,
  output [2:0] EX_Rt,
  output [15:0] EX_immediate
);

  Register #(.width(1), .trigger("falling")) register_1 (
    .D(ID_RegWrite), .en(Enable), .Q(EX_RegWrite), .clk(CLK), .clr(RST));
  Register #(.width(1), .trigger("falling")) register_2 (
    .D(ID_MemWrite), .en(Enable), .Q(EX_MemWrite), .clk(CLK), .clr(RST));
  Register #(.width(1), .trigger("falling")) register_3 (
    .D(ID_MemtoReg), .en(Enable), .Q(EX_MemtoReg), .clk(CLK), .clr(RST));
  Register #(.width(4), .trigger("falling")) register_4 (.D(ID_AluOp), .en(Enable), .Q(EX_AluOp), .clk(CLK), .clr(RST));
  Register #(.width(1), .trigger("falling")) register_5 (
    .D(ID_IMMtoALU), .en(Enable), .Q(EX_IMMtoALU), .clk(CLK), .clr(RST));
  Register #(.width(1), .trigger("falling")) register_6 (
    .D(ID_RegtoPC), .en(Enable), .Q(EX_RegtoPC), .clk(CLK), .clr(RST));
  Register #(.width(1), .trigger("falling")) register_7 (
    .D(ID_IMMtoPC), .en(Enable), .Q(EX_IMMtoPC), .clk(CLK), .clr(RST));
  Register #(.width(1), .trigger("falling")) register_8 (
    .D(ID_ZerosToALU), .en(Enable), .Q(EX_ZerosToALU), .clk(CLK), .clr(RST));
  Register #(.width(1), .trigger("falling")) register_9 (.D(ID_Halt), .en(Enable), .Q(EX_Halt), .clk(CLK), .clr(RST));
  Register #(.width(1), .trigger("falling")) register_10 (.D(ID_LED), .en(Enable), .Q(EX_LED), .clk(CLK), .clr(RST));
  Register #(.width(1), .trigger("falling")) register_11 (
    .D(ID_WriteLED), .en(Enable), .Q(EX_WriteLED), .clk(CLK), .clr(RST));
  Register #(.width(1), .trigger("falling")) register_12 (
    .D(ID_MemRead), .en(Enable), .Q(EX_MemRead), .clk(CLK), .clr(RST));
  Register #(.width(16), .trigger("falling")) register_13 (
    .D(ID_Rs_data), .en(Enable), .Q(EX_Rs_data), .clk(CLK), .clr(RST));
  Register #(.width(16), .trigger("falling")) register_14 (
    .D(ID_Rt_data), .en(Enable), .Q(EX_Rt_data), .clk(CLK), .clr(RST));
  Register #(.width(3), .trigger("falling")) register_15 (.D(ID_Rs), .en(Enable), .Q(EX_Rs), .clk(CLK), .clr(RST));
  Register #(.width(3), .trigger("falling")) register_16 (.D(ID_Rt), .en(Enable), .Q(EX_Rt), .clk(CLK), .clr(RST));
  Register #(.width(16), .trigger("falling")) register_17 (
    .D(ID_immediate), .en(Enable), .Q(EX_immediate), .clk(CLK), .clr(RST));

  // Notes on the sheet:
  //   ID/EX
endmodule

module MEM_WB_Buffer (
  input  CLK,
  input  Enable,
  input  RST,
  input  MEM_RegWrite,
  input  [15:0] MEM_MemReadData,
  input  EX_MemtoReg,
  input  [15:0] MEM_AluResult,
  input  [2:0] MEM_Rs,
  input  [2:0] MEM_Rt,
  input  MEM_Halt,
  input  MEM_LED,
  input  MEM_WriteLED,
  input  [15:0] MEM_MemWriteData,
  output WB_RegWrite,
  output [15:0] WB_MemReadData,
  output WB_MemtoReg,
  output [15:0] WB_AluResult,
  output [2:0] WB_Rs,
  output [2:0] WB_Rt,
  output WB_Halt,
  output WB_LED,
  output WB_WriteLED,
  output [15:0] WB_MemWriteData
);

  Register #(.width(1), .trigger("falling")) register_1 (
    .D(MEM_RegWrite), .en(Enable), .Q(WB_RegWrite), .clk(CLK), .clr(RST));
  Register #(.width(16), .trigger("falling")) register_2 (
    .D(MEM_MemReadData), .en(Enable), .Q(WB_MemReadData), .clk(CLK), .clr(RST));
  Register #(.width(1), .trigger("falling")) register_3 (
    .D(EX_MemtoReg), .en(Enable), .Q(WB_MemtoReg), .clk(CLK), .clr(RST));
  Register #(.width(16), .trigger("falling")) register_4 (
    .D(MEM_AluResult), .en(Enable), .Q(WB_AluResult), .clk(CLK), .clr(RST));
  Register #(.width(3), .trigger("falling")) register_5 (.D(MEM_Rs), .en(Enable), .Q(WB_Rs), .clk(CLK), .clr(RST));
  Register #(.width(3), .trigger("falling")) register_6 (.D(MEM_Rt), .en(Enable), .Q(WB_Rt), .clk(CLK), .clr(RST));
  Register #(.width(1), .trigger("falling")) register_7 (.D(MEM_Halt), .en(Enable), .Q(WB_Halt), .clk(CLK), .clr(RST));
  Register #(.width(1), .trigger("falling")) register_8 (.D(MEM_LED), .en(Enable), .Q(WB_LED), .clk(CLK), .clr(RST));
  Register #(.width(1), .trigger("falling")) register_9 (
    .D(MEM_WriteLED), .en(Enable), .Q(WB_WriteLED), .clk(CLK), .clr(RST));
  Register #(.width(16), .trigger("falling")) register_10 (
    .D(MEM_MemWriteData), .en(Enable), .Q(WB_MemWriteData), .clk(CLK), .clr(RST));

  // Notes on the sheet:
  //   MEM/WB
endmodule
